// Logisim project project_Finale.circ as structural Verilog: 55 circuits, main circuit main
module main (
  input  ONN,
  input  CHA_PIN4,
  input  CHB_PIN5,
  input  start_stop_alarm,
  input  Reset_timer,
  input  Reset_game,
  input  start_stop_stopwatch,
  input  Reset_stopwatch,
  input  start_stop_timer,
  input  Start_stop_game,
  input  ON_OFF_Music,
  input  song_selector,
  input  CH_3_Pin6,
  output Vcc,
  output PIN2_Buzzer,
  output GND
);

  wire a_HOUR_LSB, a_HOUR_MSB, a_MIN_LSB, a_MIN_MSB, a_sec_LSB, a_sec_MSB, ALARM_1_output_1, alarm_a1,
       alarm_a2, alarm_a3, alarm_a4, alarm_b1, alarm_b2, alarm_b3, alarm_b4, alarm_c1, alarm_c2, alarm_c3,
       alarm_c4, alarm_d1, alarm_d2, alarm_d3, alarm_d4, alarm_e1, alarm_e2, alarm_e3, alarm_e4, alarm_f1,
       alarm_f2, alarm_f3, alarm_f4, alarm_f5, alarm_g1, alarm_g2, alarm_g3, alarm_g4, alarm_g5, and_1_out,
       b_HOUR_LSB, b_HOUR_MSB, b_MIN_LSB, b_MIN_MSB, b_sec_LSB, b_sec_MSB, Buzzer_ALARM, Buzzer_timer,
       c_HOUR_LSB, c_HOUR_MSB, c_MIN_LSB, c_MIN_MSB, c_sec_LSB, c_sec_MSB, CCW, CLK, CW, D0, D1, D2,
       d_HOUR_LSB, d_HOUR_MSB, d_MIN_LSB, d_MIN_MSB, d_sec_LSB, d_sec_MSB, e_HOUR_LSB, e_HOUR_MSB, e_MIN_LSB,
       e_MIN_MSB, e_sec_LSB, e_sec_MSB, f_HOUR_LSB, f_HOUR_MSB, f_MIN_LSB, f_MIN_MSB, f_sec_LSB, f_sec_MSB,
       g_HOUR_LSB, g_HOUR_MSB, g_MIN_LSB, g_MIN_MSB, g_sec_LSB, g_sec_MSB, game10sec_a0, game10sec_a1,
       game10sec_a2, game10sec_a3, game10sec_a4, game10sec_a6, game10sec_b0, game10sec_b1, game10sec_b2,
       game10sec_b3, game10sec_b4, game10sec_b6, game10sec_c0, game10sec_c1, game10sec_c2, game10sec_c3,
       game10sec_c4, game10sec_c6, game10sec_d0, game10sec_d1, game10sec_d2, game10sec_d3, game10sec_d4,
       game10sec_d6, game10sec_e0, game10sec_e1, game10sec_e2, game10sec_e3, game10sec_e4, game10sec_e6,
       game10sec_f0, game10sec_f1, game10sec_f2, game10sec_f3, game10sec_f4, game10sec_f6, game10sec_g0,
       game10sec_g1, game10sec_g2, game10sec_g3, game10sec_g4, game10sec_g6, game_CLK_out, MP3_a0, MP3_a1,
       MP3_a2, MP3_a3, MP3_a4, MP3_a6, MP3_b0, MP3_b1, MP3_b2, MP3_b3, MP3_b4, MP3_b6, MP3_buzzer, MP3_c0,
       MP3_c1, MP3_c2, MP3_c3, MP3_c4, MP3_c6, MP3_d0, MP3_d1, MP3_d2, MP3_d3, MP3_d4, MP3_d6, MP3_e0,
       MP3_e1, MP3_e2, MP3_e3, MP3_e4, MP3_e6, MP3_f0, MP3_f1, MP3_f2, MP3_f3, MP3_f4, MP3_f6, MP3_g0,
       MP3_g1, MP3_g2, MP3_g3, MP3_g4, MP3_g6, multiplexer_1_out, on_off_MUSIC_t, ONN_t, or_1_out, or_2_out,
       or_3_out, or_4_out, RESET, Reset_game_t, reset_stopwatch_t, Reset_timer_t, seconds_CLK,
       song_selector_t, start_stop_alarm_t, Start_stop_game_t, start_stop_stopwatch_t, start_stop_timer_t,
       STATE_SELECTOR_BUTTON_out, state_selector_Decder_1_state1, state_selector_Decder_1_state2,
       state_selector_Decder_1_state3, state_selector_Decder_1_state4, state_selector_Decder_1_state5,
       state_selector_Decder_1_state6, state_selector_Decder_1_state7, state_selector_Decder_1_time_setting,
       stopwatch_CLK, toggle_button_1_outputtt;
  wire [4:0] ALARM_1_hours_msd;
  wire [6:0] ALARM_1_secondslsd, ALL_counter_1_hour_lsd, ALL_counter_1_hours_msd, ALL_counter_1_minlsd,
       ALL_counter_1_mins_msd, ALL_counter_1_seconds_msd, ALL_counter_1_secondslsd, Game_1_display0,
       Game_1_display1, Game_1_display2, Game_1_display3, Game_1_display4, Game_1_display5,
       stop_watch_1_display0gfedcba, stop_watch_1_display1gfedcba, stop_watch_1_display2gfedcba,
       stop_watch_1_display3gfedcba, stop_watch_1_display4gfedcba, stop_watch_1_display5gfedcba,
       Timer_1_hour_lsd, Timer_1_hours_msd, Timer_1_mins_lsd, Timer_1_mins_msd, Timer_1_seconds_lsd,
       Timer_1_seconds_msd;
  wire [20:0] ALL_counter_1_current_time;

  Clock Main_CLK (.out(CLK));
  Button u_Reset (.out(RESET));
  Button STATE_SELECTOR_BUTTON (.out(STATE_SELECTOR_BUTTON_out));
  bouncing_filter bouncing_filter_1 (.INPUT_SIGNAL(ONN), .CLK(CLK), .RESET(RESET), .SIGNAL_OUT(ONN_t));
  LED ON_OFF_LED (.in(ONN_t));
  bouncing_filter bouncing_filter_2 (
    .INPUT_SIGNAL(start_stop_alarm), .CLK(CLK), .RESET(RESET), .SIGNAL_OUT(start_stop_alarm_t));
  bouncing_filter bouncing_filter_8 (
    .INPUT_SIGNAL(Start_stop_game), .CLK(CLK), .RESET(RESET), .SIGNAL_OUT(Start_stop_game_t));
  bouncing_filter bouncing_filter_9 (
    .INPUT_SIGNAL(ON_OFF_Music), .CLK(CLK), .RESET(RESET), .SIGNAL_OUT(on_off_MUSIC_t));
  bouncing_filter bouncing_filter_10 (
    .INPUT_SIGNAL(song_selector), .CLK(CLK), .RESET(RESET), .SIGNAL_OUT(song_selector_t));
  Decoder_Rotation Decoder_Rotation_1 (.CHA(CHA_PIN4), .CHB(CHB_PIN5), .CLK(CLK), .Reset(RESET), .CCW(CCW), .CW(CW));
  toggle_button toggle_button_1 (
    .Buttonn(STATE_SELECTOR_BUTTON_out), .CLK(CLK), .Reset(RESET), .outputtt(toggle_button_1_outputtt));
  bouncing_filter bouncing_filter_3 (.INPUT_SIGNAL(Reset_timer), .CLK(CLK), .RESET(RESET), .SIGNAL_OUT(Reset_timer_t));
  bouncing_filter bouncing_filter_4 (.INPUT_SIGNAL(Reset_game), .CLK(CLK), .RESET(RESET), .SIGNAL_OUT(Reset_game_t));
  bouncing_filter bouncing_filter_5 (
    .INPUT_SIGNAL(start_stop_stopwatch), .CLK(CLK), .RESET(RESET), .SIGNAL_OUT(start_stop_stopwatch_t));
  bouncing_filter bouncing_filter_6 (
    .INPUT_SIGNAL(Reset_stopwatch), .CLK(CLK), .RESET(RESET), .SIGNAL_OUT(reset_stopwatch_t));
  bouncing_filter bouncing_filter_7 (
    .INPUT_SIGNAL(start_stop_timer), .CLK(CLK), .RESET(RESET), .SIGNAL_OUT(start_stop_timer_t));
  state_selector_FSM state_selector_FSM_1 (
    .inputtttttttttt(toggle_button_1_outputtt), .CLk(CLK), .Reset(RESET), .D2(D2), .D1(D1), .D0(D0));
  _7_Segment_Display displayy_5 (
    .g(g_HOUR_MSB), .f(f_HOUR_MSB), .a(a_HOUR_MSB), .b(b_HOUR_MSB), .e(e_HOUR_MSB), .d(d_HOUR_MSB),
    .c(c_HOUR_MSB));  // open: dp
  _7_Segment_Display displayy_4 (
    .g(g_HOUR_LSB), .f(f_HOUR_LSB), .a(a_HOUR_LSB), .b(b_HOUR_LSB), .e(e_HOUR_LSB), .d(d_HOUR_LSB),
    .c(c_HOUR_LSB));  // open: dp
  LED Time_setting_LED (.in(state_selector_Decder_1_time_setting));
  state_selector_Decder state_selector_Decder_1 (
    .D2(D2), .D1(D1), .D0(D0), .Time_setting(state_selector_Decder_1_time_setting),
    .State1(state_selector_Decder_1_state1), .State2(state_selector_Decder_1_state2),
    .State3(state_selector_Decder_1_state3), .State4(state_selector_Decder_1_state4),
    .State5(state_selector_Decder_1_state5), .state6(state_selector_Decder_1_state6),
    .State7(state_selector_Decder_1_state7));
  LED Normal_watch_mode_LED (.in(state_selector_Decder_1_state1));
  LED STOPWATCH_LED (.in(state_selector_Decder_1_state2));
  LED TIMERR_LED (.in(state_selector_Decder_1_state3));
  LED ALARMMM_LED (.in(state_selector_Decder_1_state4));
  LED state_game_LED (.in(state_selector_Decder_1_state5));
  LED MP3_LED (.in(state_selector_Decder_1_state6));
  LED game_10SECC_LED (.in(state_selector_Decder_1_state7));
  or or_1 (or_1_out, Reset_timer_t, RESET);
  _7_Segment_Display displayy_3 (
    .g(g_MIN_MSB), .f(f_MIN_MSB), .a(a_MIN_MSB), .b(b_MIN_MSB), .e(e_MIN_MSB), .d(d_MIN_MSB), .c(c_MIN_MSB));  // open: dp
  or or_2 (or_2_out, RESET, reset_stopwatch_t);
  _7_Segment_Display displayy_2 (
    .g(g_MIN_LSB), .f(f_MIN_LSB), .a(a_MIN_LSB), .b(b_MIN_LSB), .e(e_MIN_LSB), .d(d_MIN_LSB), .c(c_MIN_LSB));  // open: dp
  or or_3 (or_3_out, RESET, Reset_game_t);
  Clock #(.highDuration(32000), .lowDuration(32000)) clock_1 (.out(seconds_CLK));
  Clock #(.highDuration(320), .lowDuration(320)) clock_2 (.out(stopwatch_CLK));
  _7_Segment_Display displayy_1 (
    .g(g_sec_MSB), .f(f_sec_MSB), .a(a_sec_MSB), .b(b_sec_MSB), .e(e_sec_MSB), .d(d_sec_MSB), .c(c_sec_MSB));  // open: dp
  _7_Segment_Display displayy_0 (
    .g(g_sec_LSB), .f(f_sec_LSB), .a(a_sec_LSB), .b(b_sec_LSB), .e(e_sec_LSB), .d(d_sec_LSB), .c(c_sec_LSB));  // open: dp
  or or_4 (or_4_out, RESET, Reset_game_t);
  and and_1 (and_1_out, ONN_t, Start_stop_game_t);
  Clock #(.highDuration(32000), .lowDuration(32000)) game_CLK (.out(game_CLK_out));
  ALARM ALARM_1 (
    .current_time(ALL_counter_1_current_time), .ONN(ONN_t), .State_ALARM(state_selector_Decder_1_state4),
    .START_STOP_ALARM(start_stop_alarm_t), .CW(CW), .CWW(CCW), .Reset(RESET), .Seconds_clk(CLK),
    .CLK64Khz(seconds_CLK), .secondsLSD(ALARM_1_secondslsd),
    .Seconds_MSD({alarm_g1, alarm_f1, alarm_e1, alarm_d1, alarm_c1, alarm_b1, alarm_a1}),
    .MinLSD({alarm_g2, alarm_f2, alarm_e2, alarm_d2, alarm_c2, alarm_b2, alarm_a2}),
    .MINs_MSD({alarm_g3, alarm_f3, alarm_e3, alarm_d3, alarm_c3, alarm_b3, alarm_a3}),
    .HOUR_LSD({alarm_g4, alarm_f4, alarm_e4, alarm_d4, alarm_c4, alarm_b4, alarm_a4}),
    .HOURS_MSD({alarm_g5, alarm_f5, ALARM_1_hours_msd}), .Beep(Buzzer_ALARM), .Output_1(ALARM_1_output_1));
  game10sec game10sec_1 (
    .START1_STOP0(Start_stop_game_t), .Reset(or_3_out), .FASTEST_CLK(stopwatch_CLK),
    .State7(state_selector_Decder_1_state7),
    .display5({game10sec_g6, game10sec_f6, game10sec_e6, game10sec_d6, game10sec_c6, game10sec_b6, game10sec_a6}),
    .display4({game10sec_g4, game10sec_f4, game10sec_e4, game10sec_d4, game10sec_c4, game10sec_b4, game10sec_a4}),
    .display3({game10sec_g3, game10sec_f3, game10sec_e3, game10sec_d3, game10sec_c3, game10sec_b3, game10sec_a3}),
    .display2({game10sec_g2, game10sec_f2, game10sec_e2, game10sec_d2, game10sec_c2, game10sec_b2, game10sec_a2}),
    .display1({game10sec_g1, game10sec_f1, game10sec_e1, game10sec_d1, game10sec_c1, game10sec_b1, game10sec_a1}),
    .display0({game10sec_g0, game10sec_f0, game10sec_e0, game10sec_d0, game10sec_c0, game10sec_b0, game10sec_a0}));
  ALL_counter ALL_counter_1 (
    .State0(state_selector_Decder_1_time_setting), .CW(CW), .CWW(CCW), .ONN(ONN_t), .Reset(RESET),
    .CLK_seconds(seconds_CLK), .CLK_64KHz(CLK), .secondsLSD(ALL_counter_1_secondslsd),
    .Seconds_MSD(ALL_counter_1_seconds_msd), .MinLSD(ALL_counter_1_minlsd),
    .MINs_MSD(ALL_counter_1_mins_msd), .HOUR_LSD(ALL_counter_1_hour_lsd),
    .HOURS_MSD(ALL_counter_1_hours_msd), .current_time(ALL_counter_1_current_time));
  LED ALARM_ON_LED (.in(ALARM_1_output_1));
  stop_watch stop_watch_1 (
    .START1_STOP0(start_stop_stopwatch_t), .Reset(or_2_out), .FASTEST_CLK(stopwatch_CLK),
    .State2(state_selector_Decder_1_state2), .display0gfedcba(stop_watch_1_display0gfedcba),
    .display1gfedcba(stop_watch_1_display1gfedcba), .display2gfedcba(stop_watch_1_display2gfedcba),
    .display3gfedcba(stop_watch_1_display3gfedcba), .display4gfedcba(stop_watch_1_display4gfedcba),
    .display5gfedcba(stop_watch_1_display5gfedcba));
  Timer Timer_1 (
    .State3(state_selector_Decder_1_state3), .start_stop_timer(start_stop_timer_t), .CW(CW), .CWW(CCW),
    .ONN(ONN_t), .Reset(or_1_out), .seconds_CLK(seconds_CLK), .CLK_64KHz(CLK), .confirm(CH_3_Pin6),
    .seconds_LSD(Timer_1_seconds_lsd), .SECONDS_MSD(Timer_1_seconds_msd), .MINS_LSD(Timer_1_mins_lsd),
    .MINS_MSD(Timer_1_mins_msd), .HOUR_LSD(Timer_1_hour_lsd), .HOURS_MSD(Timer_1_hours_msd),
    .BUZZER_ON(Buzzer_timer));
  Game Game_1 (
    .Cw(CW), .CCW(CCW), .Reset_game(or_4_out), .start_stop(and_1_out),
    .state_game(state_selector_Decder_1_state5), .CLK(game_CLK_out), .display0(Game_1_display0),
    .display1(Game_1_display1), .display2(Game_1_display2), .display3(Game_1_display3),
    .display4(Game_1_display4), .display5(Game_1_display5));
  MP3 MP3_1 (
    .state_MP3(state_selector_Decder_1_state6), .ON_OFF_MUSIC(on_off_MUSIC_t),
    .SONG_SELECTOR(song_selector_t), .pin2_buzzer(MP3_buzzer),
    .display5({MP3_g6, MP3_f6, MP3_e6, MP3_d6, MP3_c6, MP3_b6, MP3_a6}),
    .display4({MP3_g4, MP3_f4, MP3_e4, MP3_d4, MP3_c4, MP3_b4, MP3_a4}),
    .display3({MP3_g3, MP3_f3, MP3_e3, MP3_d3, MP3_c3, MP3_b3, MP3_a3}),
    .display2({MP3_g2, MP3_f2, MP3_e2, MP3_d2, MP3_c2, MP3_b2, MP3_a2}),
    .display1({MP3_g1, MP3_f1, MP3_e1, MP3_d1, MP3_c1, MP3_b1, MP3_a1}),
    .display0({MP3_g0, MP3_f0, MP3_e0, MP3_d0, MP3_c0, MP3_b0, MP3_a0}));
  Multiplexer #(.select(3)) multiplexer_1 (
    .in0(1'b0), .in1(1'b0), .in2(1'b0), .in3(Buzzer_timer), .in4(Buzzer_ALARM), .in5(1'b0), .in6(MP3_buzzer),
    .in7(1'b0), .out(multiplexer_1_out), .sel({D2, D1, D0}));
  or or_5 (PIN2_Buzzer, Buzzer_ALARM, multiplexer_1_out);
  display_selector DISPLAY0 (
    .a_func0(ALL_counter_1_secondslsd[0]), .a_func1(ALL_counter_1_secondslsd[0]),
    .a_func2(stop_watch_1_display0gfedcba[0]), .a_func3(Timer_1_seconds_lsd[0]),
    .a_func4(ALARM_1_secondslsd[0]), .a_func5(Game_1_display0[0]), .a_func6(MP3_a0), .a_func7(game10sec_a0),
    .b_func0(ALL_counter_1_secondslsd[1]), .b_func1(ALL_counter_1_secondslsd[1]),
    .b_func2(stop_watch_1_display0gfedcba[1]), .b_func3(Timer_1_seconds_lsd[1]),
    .b_func4(ALARM_1_secondslsd[1]), .b_func5(Game_1_display0[1]), .b_func6(MP3_b0), .b_func7(game10sec_b0),
    .c_func0(ALL_counter_1_secondslsd[2]), .c_func1(ALL_counter_1_secondslsd[2]),
    .c_func2(stop_watch_1_display0gfedcba[2]), .c_func3(Timer_1_seconds_lsd[2]),
    .c_func4(ALARM_1_secondslsd[2]), .c_func5(Game_1_display0[2]), .c_func6(MP3_c0), .c_func7(game10sec_c0),
    .d_func0(ALL_counter_1_secondslsd[3]), .d_func1(ALL_counter_1_secondslsd[3]),
    .d_func2(stop_watch_1_display0gfedcba[3]), .d_func3(Timer_1_seconds_lsd[3]),
    .d_func4(ALARM_1_secondslsd[3]), .d_func5(Game_1_display0[3]), .d_func6(MP3_d0), .d_func7(game10sec_d0),
    .e_func0(ALL_counter_1_secondslsd[4]), .e_func1(ALL_counter_1_secondslsd[4]),
    .e_func2(stop_watch_1_display0gfedcba[4]), .e_func3(Timer_1_seconds_lsd[4]),
    .e_func4(ALARM_1_secondslsd[4]), .e_func5(Game_1_display0[4]), .e_func6(MP3_e0), .e_func7(game10sec_e0),
    .f_func0(ALL_counter_1_secondslsd[5]), .f_func1(ALL_counter_1_secondslsd[5]),
    .f_func2(stop_watch_1_display0gfedcba[5]), .f_func3(Timer_1_seconds_lsd[5]),
    .f_func4(ALARM_1_secondslsd[5]), .f_func5(Game_1_display0[5]), .f_func6(MP3_f0), .f_func7(game10sec_f0),
    .g_func0(ALL_counter_1_secondslsd[6]), .g_func1(ALL_counter_1_secondslsd[6]),
    .g_func2(stop_watch_1_display0gfedcba[6]), .g_func3(Timer_1_seconds_lsd[6]),
    .g_func4(ALARM_1_secondslsd[6]), .g_func5(Game_1_display0[6]), .g_func6(MP3_g0), .g_func7(game10sec_g0),
    .D2(D2), .D1(D1), .D0(D0), .a_display(a_sec_LSB), .b_display(b_sec_LSB), .c_display(c_sec_LSB),
    .d_display(d_sec_LSB), .e_display(e_sec_LSB), .f_display(f_sec_LSB), .g_display(g_sec_LSB));
  display_selector DIsplay1 (
    .a_func0(ALL_counter_1_seconds_msd[0]), .a_func1(ALL_counter_1_seconds_msd[0]),
    .a_func2(stop_watch_1_display1gfedcba[0]), .a_func3(Timer_1_seconds_msd[0]), .a_func4(alarm_a1),
    .a_func5(Game_1_display1[0]), .a_func6(MP3_a1), .a_func7(game10sec_a1),
    .b_func0(ALL_counter_1_seconds_msd[1]), .b_func1(ALL_counter_1_seconds_msd[1]),
    .b_func2(stop_watch_1_display1gfedcba[1]), .b_func3(Timer_1_seconds_msd[1]), .b_func4(alarm_b1),
    .b_func5(Game_1_display1[1]), .b_func6(MP3_b1), .b_func7(game10sec_b1),
    .c_func0(ALL_counter_1_seconds_msd[2]), .c_func1(ALL_counter_1_seconds_msd[2]),
    .c_func2(stop_watch_1_display1gfedcba[2]), .c_func3(Timer_1_seconds_msd[2]), .c_func4(alarm_c1),
    .c_func5(Game_1_display1[2]), .c_func6(MP3_c1), .c_func7(game10sec_c1),
    .d_func0(ALL_counter_1_seconds_msd[3]), .d_func1(ALL_counter_1_seconds_msd[3]),
    .d_func2(stop_watch_1_display1gfedcba[3]), .d_func3(Timer_1_seconds_msd[3]), .d_func4(alarm_d1),
    .d_func5(Game_1_display1[3]), .d_func6(MP3_d1), .d_func7(game10sec_d1),
    .e_func0(ALL_counter_1_seconds_msd[4]), .e_func1(ALL_counter_1_seconds_msd[4]),
    .e_func2(stop_watch_1_display1gfedcba[4]), .e_func3(Timer_1_seconds_msd[4]), .e_func4(alarm_e1),
    .e_func5(Game_1_display1[4]), .e_func6(MP3_e1), .e_func7(game10sec_e1),
    .f_func0(ALL_counter_1_seconds_msd[5]), .f_func1(ALL_counter_1_seconds_msd[5]),
    .f_func2(stop_watch_1_display1gfedcba[5]), .f_func3(Timer_1_seconds_msd[5]), .f_func4(alarm_f1),
    .f_func5(Game_1_display1[5]), .f_func6(MP3_f1), .f_func7(game10sec_f1),
    .g_func0(ALL_counter_1_seconds_msd[6]), .g_func1(ALL_counter_1_seconds_msd[6]),
    .g_func2(stop_watch_1_display1gfedcba[6]), .g_func3(Timer_1_seconds_msd[6]), .g_func4(alarm_g1),
    .g_func5(Game_1_display1[6]), .g_func6(MP3_g1), .g_func7(game10sec_g1), .D2(D2), .D1(D1), .D0(D0),
    .a_display(a_sec_MSB), .b_display(b_sec_MSB), .c_display(c_sec_MSB), .d_display(d_sec_MSB),
    .e_display(e_sec_MSB), .f_display(f_sec_MSB), .g_display(g_sec_MSB));
  display_selector Display2 (
    .a_func0(ALL_counter_1_minlsd[0]), .a_func1(ALL_counter_1_minlsd[0]),
    .a_func2(stop_watch_1_display2gfedcba[0]), .a_func3(Timer_1_mins_lsd[0]), .a_func4(alarm_a2),
    .a_func5(Game_1_display2[0]), .a_func6(MP3_a2), .a_func7(game10sec_a2),
    .b_func0(ALL_counter_1_minlsd[1]), .b_func1(ALL_counter_1_minlsd[1]),
    .b_func2(stop_watch_1_display2gfedcba[1]), .b_func3(Timer_1_mins_lsd[1]), .b_func4(alarm_b2),
    .b_func5(Game_1_display2[1]), .b_func6(MP3_b2), .b_func7(game10sec_b2),
    .c_func0(ALL_counter_1_minlsd[2]), .c_func1(ALL_counter_1_minlsd[2]),
    .c_func2(stop_watch_1_display2gfedcba[2]), .c_func3(Timer_1_mins_lsd[2]), .c_func4(alarm_c2),
    .c_func5(Game_1_display2[2]), .c_func6(MP3_c2), .c_func7(game10sec_c2),
    .d_func0(ALL_counter_1_minlsd[3]), .d_func1(ALL_counter_1_minlsd[3]),
    .d_func2(stop_watch_1_display2gfedcba[3]), .d_func3(Timer_1_mins_lsd[3]), .d_func4(alarm_d2),
    .d_func5(Game_1_display2[3]), .d_func6(MP3_d2), .d_func7(game10sec_d2),
    .e_func0(ALL_counter_1_minlsd[4]), .e_func1(ALL_counter_1_minlsd[4]),
    .e_func2(stop_watch_1_display2gfedcba[4]), .e_func3(Timer_1_mins_lsd[4]), .e_func4(alarm_e2),
    .e_func5(Game_1_display2[4]), .e_func6(MP3_e2), .e_func7(game10sec_e2),
    .f_func0(ALL_counter_1_minlsd[5]), .f_func1(ALL_counter_1_minlsd[5]),
    .f_func2(stop_watch_1_display2gfedcba[5]), .f_func3(Timer_1_mins_lsd[5]), .f_func4(alarm_f2),
    .f_func5(Game_1_display2[5]), .f_func6(MP3_f2), .f_func7(game10sec_f2),
    .g_func0(ALL_counter_1_minlsd[6]), .g_func1(ALL_counter_1_minlsd[6]),
    .g_func2(stop_watch_1_display2gfedcba[6]), .g_func3(Timer_1_mins_lsd[6]), .g_func4(alarm_g2),
    .g_func5(Game_1_display2[6]), .g_func6(MP3_g2), .g_func7(game10sec_g2), .D2(D2), .D1(D1), .D0(D0),
    .a_display(a_MIN_LSB), .b_display(b_MIN_LSB), .c_display(c_MIN_LSB), .d_display(d_MIN_LSB),
    .e_display(e_MIN_LSB), .f_display(f_MIN_LSB), .g_display(g_MIN_LSB));
  display_selector display3 (
    .a_func0(ALL_counter_1_mins_msd[0]), .a_func1(ALL_counter_1_mins_msd[0]),
    .a_func2(stop_watch_1_display3gfedcba[0]), .a_func3(Timer_1_mins_msd[0]), .a_func4(alarm_a3),
    .a_func5(Game_1_display3[0]), .a_func6(MP3_a3), .a_func7(game10sec_a3),
    .b_func0(ALL_counter_1_mins_msd[1]), .b_func1(ALL_counter_1_mins_msd[1]),
    .b_func2(stop_watch_1_display3gfedcba[1]), .b_func3(Timer_1_mins_msd[1]), .b_func4(alarm_b3),
    .b_func5(Game_1_display3[1]), .b_func6(MP3_b3), .b_func7(game10sec_b3),
    .c_func0(ALL_counter_1_mins_msd[2]), .c_func1(ALL_counter_1_mins_msd[2]),
    .c_func2(stop_watch_1_display3gfedcba[2]), .c_func3(Timer_1_mins_msd[2]), .c_func4(alarm_c3),
    .c_func5(Game_1_display3[2]), .c_func6(MP3_c3), .c_func7(game10sec_c3),
    .d_func0(ALL_counter_1_mins_msd[3]), .d_func1(ALL_counter_1_mins_msd[3]),
    .d_func2(stop_watch_1_display3gfedcba[3]), .d_func3(Timer_1_mins_msd[3]), .d_func4(alarm_d3),
    .d_func5(Game_1_display3[3]), .d_func6(MP3_d3), .d_func7(game10sec_d3),
    .e_func0(ALL_counter_1_mins_msd[4]), .e_func1(ALL_counter_1_mins_msd[4]),
    .e_func2(stop_watch_1_display3gfedcba[4]), .e_func3(Timer_1_mins_msd[4]), .e_func4(alarm_e3),
    .e_func5(Game_1_display3[4]), .e_func6(MP3_e3), .e_func7(game10sec_e3),
    .f_func0(ALL_counter_1_mins_msd[5]), .f_func1(ALL_counter_1_mins_msd[5]),
    .f_func2(stop_watch_1_display3gfedcba[5]), .f_func3(Timer_1_mins_msd[5]), .f_func4(alarm_f3),
    .f_func5(Game_1_display3[5]), .f_func6(MP3_f3), .f_func7(game10sec_f3),
    .g_func0(ALL_counter_1_mins_msd[6]), .g_func1(ALL_counter_1_mins_msd[6]),
    .g_func2(stop_watch_1_display3gfedcba[6]), .g_func3(Timer_1_mins_msd[6]), .g_func4(alarm_g3),
    .g_func5(Game_1_display3[6]), .g_func6(MP3_g3), .g_func7(game10sec_g3), .D2(D2), .D1(D1), .D0(D0),
    .a_display(a_MIN_MSB), .b_display(b_MIN_MSB), .c_display(c_MIN_MSB), .d_display(d_MIN_MSB),
    .e_display(e_MIN_MSB), .f_display(f_MIN_MSB), .g_display(g_MIN_MSB));
  display_selector display4 (
    .a_func0(ALL_counter_1_hour_lsd[0]), .a_func1(ALL_counter_1_hour_lsd[0]),
    .a_func2(stop_watch_1_display4gfedcba[0]), .a_func3(Timer_1_hour_lsd[0]), .a_func4(alarm_a4),
    .a_func5(Game_1_display4[0]), .a_func6(MP3_a4), .a_func7(game10sec_a4),
    .b_func0(ALL_counter_1_hour_lsd[1]), .b_func1(ALL_counter_1_hour_lsd[1]),
    .b_func2(stop_watch_1_display4gfedcba[1]), .b_func3(Timer_1_hour_lsd[1]), .b_func4(alarm_b4),
    .b_func5(Game_1_display4[1]), .b_func6(MP3_b4), .b_func7(game10sec_b4),
    .c_func0(ALL_counter_1_hour_lsd[2]), .c_func1(ALL_counter_1_hour_lsd[2]),
    .c_func2(stop_watch_1_display4gfedcba[2]), .c_func3(Timer_1_hour_lsd[2]), .c_func4(alarm_c4),
    .c_func5(Game_1_display4[2]), .c_func6(MP3_c4), .c_func7(game10sec_c4),
    .d_func0(ALL_counter_1_hour_lsd[3]), .d_func1(ALL_counter_1_hour_lsd[3]),
    .d_func2(stop_watch_1_display4gfedcba[3]), .d_func3(Timer_1_hour_lsd[3]), .d_func4(alarm_d4),
    .d_func5(Game_1_display4[3]), .d_func6(MP3_d4), .d_func7(game10sec_d4),
    .e_func0(ALL_counter_1_hour_lsd[4]), .e_func1(ALL_counter_1_hour_lsd[4]),
    .e_func2(stop_watch_1_display4gfedcba[4]), .e_func3(Timer_1_hour_lsd[4]), .e_func4(alarm_e4),
    .e_func5(Game_1_display4[4]), .e_func6(MP3_e4), .e_func7(game10sec_e4),
    .f_func0(ALL_counter_1_hour_lsd[5]), .f_func1(ALL_counter_1_hour_lsd[5]),
    .f_func2(stop_watch_1_display4gfedcba[5]), .f_func3(Timer_1_hour_lsd[5]), .f_func4(alarm_f4),
    .f_func5(Game_1_display4[5]), .f_func6(MP3_f4), .f_func7(game10sec_f4),
    .g_func0(ALL_counter_1_hour_lsd[6]), .g_func1(ALL_counter_1_hour_lsd[6]),
    .g_func2(stop_watch_1_display4gfedcba[6]), .g_func3(Timer_1_hour_lsd[6]), .g_func4(alarm_g4),
    .g_func5(Game_1_display4[6]), .g_func6(MP3_g4), .g_func7(game10sec_g4), .D2(D2), .D1(D1), .D0(D0),
    .a_display(a_HOUR_LSB), .b_display(b_HOUR_LSB), .c_display(c_HOUR_LSB), .d_display(d_HOUR_LSB),
    .e_display(e_HOUR_LSB), .f_display(f_HOUR_LSB), .g_display(g_HOUR_LSB));
  display_selector display5 (
    .a_func0(ALL_counter_1_hours_msd[0]), .a_func1(ALL_counter_1_hours_msd[0]),
    .a_func2(stop_watch_1_display5gfedcba[0]), .a_func3(Timer_1_hours_msd[0]),
    .a_func4(ALARM_1_hours_msd[0]), .a_func5(Game_1_display5[0]), .a_func6(MP3_a6), .a_func7(game10sec_a6),
    .b_func0(ALL_counter_1_hours_msd[1]), .b_func1(ALL_counter_1_hours_msd[1]),
    .b_func2(stop_watch_1_display5gfedcba[1]), .b_func3(Timer_1_hours_msd[1]),
    .b_func4(ALARM_1_hours_msd[1]), .b_func5(Game_1_display5[1]), .b_func6(MP3_b6), .b_func7(game10sec_b6),
    .c_func0(ALL_counter_1_hours_msd[2]), .c_func1(ALL_counter_1_hours_msd[2]),
    .c_func2(stop_watch_1_display5gfedcba[2]), .c_func3(Timer_1_hours_msd[2]),
    .c_func4(ALARM_1_hours_msd[2]), .c_func5(Game_1_display5[2]), .c_func6(MP3_c6), .c_func7(game10sec_c6),
    .d_func0(ALL_counter_1_hours_msd[3]), .d_func1(ALL_counter_1_hours_msd[3]),
    .d_func2(stop_watch_1_display5gfedcba[3]), .d_func3(Timer_1_hours_msd[3]),
    .d_func4(ALARM_1_hours_msd[3]), .d_func5(Game_1_display5[3]), .d_func6(MP3_d6), .d_func7(game10sec_d6),
    .e_func0(ALL_counter_1_hours_msd[4]), .e_func1(ALL_counter_1_hours_msd[4]),
    .e_func2(stop_watch_1_display5gfedcba[4]), .e_func3(Timer_1_hours_msd[4]),
    .e_func4(ALARM_1_hours_msd[4]), .e_func5(Game_1_display5[4]), .e_func6(MP3_e6), .e_func7(game10sec_e6),
    .f_func0(ALL_counter_1_hours_msd[5]), .f_func1(ALL_counter_1_hours_msd[5]),
    .f_func2(stop_watch_1_display5gfedcba[5]), .f_func3(Timer_1_hours_msd[5]), .f_func4(alarm_f5),
    .f_func5(Game_1_display5[5]), .f_func6(MP3_f6), .f_func7(game10sec_f6),
    .g_func0(ALL_counter_1_hours_msd[6]), .g_func1(ALL_counter_1_hours_msd[6]),
    .g_func2(stop_watch_1_display5gfedcba[6]), .g_func3(Timer_1_hours_msd[6]), .g_func4(alarm_g5),
    .g_func5(Game_1_display5[6]), .g_func6(MP3_g6), .g_func7(game10sec_g6), .D2(D2), .D1(D1), .D0(D0),
    .a_display(a_HOUR_MSB), .b_display(b_HOUR_MSB), .c_display(c_HOUR_MSB), .d_display(d_HOUR_MSB),
    .e_display(e_HOUR_MSB), .f_display(f_HOUR_MSB), .g_display(g_HOUR_MSB));

  assign GND = 1'b0;
  assign Vcc = 1'b1;

  // Other names for the same wires on the sheet: confirmmm = CH_3_Pin6

  // Notes on the sheet:
  //   filtred inside the toggle button 
  //   no filter needed pre filtred button
  //   prefiltred button
  //   no filter needed pre filtred button
  //   1 if watch os ON, 0 if watch is OFF
  //   both games have the same start_stop and reset
  //   MP3
  //   10sec game
  //   alarm
  //   Game
  //   timer_seconds_LSD
  //   pour controller a b c d e f g des 6 "7-segment" display
  //   stopwatch
  //   normal_mode
  //   display_0
  //   timer
  //   alarm
  //   stopwatch
  //   game
  //   display1
  //   game
  //   stopwatch
  //   timer
  //   alarm
  //   display2
  //   alarm
  //   game
  //   stopwatch
  //   timer
  //   display3
  //   game
  //   timer
  //   stopwatch
  //   alarm
  //   display4
  //   MP3
  //   10 sec game
  //   game
  //   alarm
  //   stomwatch
  //   timer
  //   display5
endmodule

// 0-9 counter
module counter09 (
  input  Enable,
  input  CLK,
  input  Reset,
  input  increment,
  output D0,
  output D1,
  output D2,
  output D3,
  output cout
);

  wire d_ff_1_qn, d_ff_2_qn, d_ff_3_qn, d_ff_4_qn, transition_logic_09_1_d0, transition_logic_09_1_d1,
       transition_logic_09_1_d2, transition_logic_09_1_d3;

  transition_logic_09 transition_logic_09_1 (
    .C0(D0), .C1(D1), .C2(D2), .C3(D3), .Enable(Enable), .increment(increment),
    .D0(transition_logic_09_1_d0), .D1(transition_logic_09_1_d1), .D2(transition_logic_09_1_d2),
    .D3(transition_logic_09_1_d3), .cout(cout));
  D_Flip_Flop d_ff_1 (.D(transition_logic_09_1_d1), .clk(CLK), .Q(D1), .Qn(d_ff_1_qn), .reset(Reset));  // open: preset
  D_Flip_Flop d_ff_2 (.D(transition_logic_09_1_d2), .clk(CLK), .Q(D2), .Qn(d_ff_2_qn), .reset(Reset));  // open: preset
  D_Flip_Flop d_ff_3 (.D(transition_logic_09_1_d3), .clk(CLK), .Q(D3), .Qn(d_ff_3_qn), .reset(Reset));  // open: preset
  D_Flip_Flop d_ff_4 (.D(transition_logic_09_1_d0), .clk(CLK), .Q(D0), .Qn(d_ff_4_qn), .reset(Reset));  // open: preset
  // NoConnect on d_ff_4_qn
  // NoConnect on d_ff_1_qn
  // NoConnect on d_ff_2_qn
  // NoConnect on d_ff_3_qn
endmodule

module transition_logic_09 (
  input  C0,
  input  C1,
  input  C2,
  input  C3,
  input  Enable,
  input  increment,
  output D0,
  output D1,
  output D2,
  output D3,
  output cout
);

  wire and_1_out, and_2_out, and_3_out, and_4_out, and_5_out, and_6_out, and_7_out, and_8_out, and_9_out,
       and_10_out, and_11_out, and_12_out, and_13_out, and_14_out, and_15_out, and_16_out, and_17_out,
       and_18_out, and_19_out, and_20_out, and_21_out, and_22_out, and_23_out, and_24_out, and_25_out,
       and_26_out, and_27_out, not_1_out, not_2_out, not_3_out, not_4_out, not_5_out, not_6_out;

  not not_1 (not_1_out, Enable);
  not not_2 (not_2_out, increment);
  not not_3 (not_3_out, C0);
  not not_4 (not_4_out, C1);
  not not_5 (not_5_out, C2);
  not not_6 (not_6_out, C3);
  and and_1 (and_1_out, increment, C1, C2, C3, Enable);
  and and_2 (and_2_out, increment, C0, not_6_out);
  and and_3 (and_3_out, C0, not_1_out);
  and and_4 (and_4_out, not_2_out, not_3_out, not_4_out, not_5_out, not_6_out, Enable);
  and and_5 (and_5_out, not_2_out, C0, not_4_out, not_5_out, C3);
  and and_6 (and_6_out, C0, C2, not_6_out);
  and and_7 (and_7_out, C0, C1, not_6_out);
  and and_8 (and_8_out, C0, C1, C2);
  and and_9 (and_9_out, not_4_out, C2, C3, Enable, increment);
  and and_10 (and_10_out, C1, not_1_out);
  and and_11 (and_11_out, C0, not_5_out, not_6_out, Enable, not_2_out);
  and and_12 (and_12_out, C0, not_4_out, C2, C3, Enable);
  and and_13 (and_13_out, C1, not_5_out, C3);
  and and_14 (and_14_out, C1, not_6_out, increment);
  and and_15 (and_15_out, C1, C2, not_6_out);
  and and_16 (and_16_out, not_3_out, C1, C2, not_2_out);
  and and_17 (and_17_out, not_1_out, C2);
  and and_18 (and_18_out, not_2_out, not_3_out, C2, C3);
  and and_19 (and_19_out, Enable, not_2_out, not_3_out, C1, not_5_out, not_6_out);
  and and_20 (and_20_out, Enable, not_2_out, C0, not_4_out, not_6_out);
  and and_21 (and_21_out, C0, C2, not_6_out);
  and and_22 (and_22_out, Enable, increment, not_3_out, not_5_out, C3);
  and and_23 (and_23_out, increment, C2, not_6_out);
  and and_24 (and_24_out, not_1_out, C3);
  and and_25 (and_25_out, Enable, not_6_out);
  and and_26 (and_26_out, not_2_out, not_3_out, not_4_out, not_5_out, not_6_out, Enable);
  and and_27 (and_27_out, increment, C0, not_4_out, not_5_out, C3, Enable);
  or or_1 (D0, and_1_out, and_2_out, and_3_out, and_4_out, and_5_out, and_6_out, and_7_out, and_8_out);
  or or_2 (D1, and_9_out, and_10_out, and_11_out, and_12_out, and_13_out, and_14_out, and_15_out, and_16_out);
  or or_3 (D2, and_17_out, and_18_out, and_19_out, and_20_out, and_21_out, and_22_out, and_23_out);
  or or_4 (D3, and_24_out, and_25_out);
  or or_5 (cout, and_26_out, and_27_out);
endmodule

// display decoder
module seven_segment_display_decoder (
  input  w,
  input  x,
  input  y,
  input  z,
  output a,
  output b,
  output c,
  output d,
  output e,
  output f,
  output g
);

  wire and_1_out, and_2_out, and_3_out, and_4_out, and_5_out, and_6_out, and_7_out, and_8_out, and_9_out,
       and_10_out, and_11_out, and_12_out, and_13_out, and_14_out, and_15_out, and_16_out, and_17_out,
       and_18_out, and_19_out, and_20_out, and_21_out, and_22_out, and_23_out, and_24_out, and_25_out,
       and_26_out, and_27_out, and_28_out, and_29_out, and_30_out, and_31_out, and_32_out, and_33_out,
       and_34_out, and_35_out, not_1_out, not_2_out, not_3_out, not_4_out;

  not not_1 (not_1_out, w);
  not not_2 (not_2_out, x);
  not not_3 (not_3_out, y);
  not not_4 (not_4_out, z);
  and and_1 (and_1_out, not_2_out, not_4_out);
  and and_2 (and_2_out, not_1_out, y);
  and and_3 (and_3_out, not_1_out, x, z);
  and and_4 (and_4_out, w, not_2_out, not_3_out);
  and and_5 (and_5_out, w, not_4_out);
  and and_6 (and_6_out, x, y);
  and and_7 (and_7_out, not_1_out, not_3_out, not_4_out);
  and and_8 (and_8_out, not_1_out, y, z);
  and and_9 (and_9_out, w, not_3_out, z);
  and and_10 (and_10_out, not_2_out, not_3_out);
  and and_11 (and_11_out, not_2_out, not_4_out);
  and and_12 (and_12_out, not_1_out, x);
  and and_13 (and_13_out, w, not_2_out);
  and and_14 (and_14_out, not_3_out, z);
  and and_15 (and_15_out, not_2_out, not_3_out);
  and and_16 (and_16_out, not_2_out, z);
  and and_17 (and_17_out, x, not_3_out, z);
  and and_18 (and_18_out, not_1_out, not_2_out, not_4_out);
  and and_19 (and_19_out, not_2_out, y, z);
  and and_20 (and_20_out, w, not_3_out);
  and and_21 (and_21_out, x, y, not_4_out);
  and and_22 (and_22_out, not_2_out, not_4_out);
  and and_23 (and_23_out, y, not_4_out);
  and and_24 (and_24_out, w, y);
  and and_25 (and_25_out, w, x);
  and and_26 (and_26_out, not_3_out, not_4_out);
  and and_27 (and_27_out, not_1_out, x, not_3_out);
  and and_28 (and_28_out, x, not_4_out);
  and and_29 (and_29_out, w, not_2_out);
  and and_30 (and_30_out, w, y);
  and and_31 (and_31_out, not_2_out, y);
  and and_32 (and_32_out, w, not_2_out);
  and and_33 (and_33_out, not_1_out, x, not_3_out);
  and and_34 (and_34_out, y, not_4_out);
  and and_35 (and_35_out, w, z);
  or or_1 (a, and_1_out, and_2_out, and_3_out, and_4_out, and_5_out, and_6_out);
  or or_2 (b, and_7_out, and_8_out, and_9_out, and_10_out, and_11_out);
  or or_3 (c, and_12_out, and_13_out, and_14_out, and_15_out, and_16_out);
  or or_4 (d, and_17_out, and_18_out, and_19_out, and_20_out, and_21_out);
  or or_5 (e, and_22_out, and_23_out, and_24_out, and_25_out);
  or or_6 (f, and_26_out, and_27_out, and_28_out, and_29_out, and_30_out);
  or or_7 (g, and_31_out, and_32_out, and_33_out, and_34_out, and_35_out);

  // Notes on the sheet:
  //   VOIR TP3, decoder wxyz vers abcdefg for the 7 segment display
endmodule

// Main_TIME_COUNTER
module ALL_counter (
  input  State0,
  input  CW,
  input  CWW,
  input  ONN,
  input  Reset,
  input  CLK_seconds,
  input  CLK_64KHz,
  output [6:0] secondsLSD,
  output [6:0] Seconds_MSD,
  output [6:0] MinLSD,
  output [6:0] MINs_MSD,
  output [6:0] HOUR_LSD,
  output [6:0] HOURS_MSD,
  output [20:0] current_time
);

  wire counter05_1_cout, counter05_2_cout, counter09_1_cout, counter09_2_cout, counter24h_1_cout,
       ENable_gate_out, glitch_free_mux_v2_1_clk_out, or_1_out, setting_timeee_1_enable,
       setting_timeee_1_increment;

  or or_1 (or_1_out, ~State0, ONN);  // OR_Gate
  glitch_free_mux_v2 glitch_free_mux_v2_1 (
    .SELECTT(or_1_out), .CLK1(CLK_seconds), .CLK0(CLK_64KHz), .Reset(Reset),
    .CLK_OUT(glitch_free_mux_v2_1_clk_out));
  setting_timeee setting_timeee_1 (
    .State0(State0), .Cw(CW), .CCw(CWW), .Onn(ONN), .increment(setting_timeee_1_increment),
    .Enable(setting_timeee_1_enable));
  or ENable_gate (ENable_gate_out, setting_timeee_1_enable, ONN);
  counter09 counter09_2 (
    .Enable(counter05_1_cout), .CLK(glitch_free_mux_v2_1_clk_out), .Reset(Reset),
    .increment(setting_timeee_1_increment), .D0(current_time[8]), .D1(current_time[9]),
    .D2(current_time[10]), .D3(current_time[11]), .cout(counter09_2_cout));
  counter05 counter05_2 (
    .Enable(counter09_2_cout), .CLK(glitch_free_mux_v2_1_clk_out), .Reset(Reset),
    .increment(setting_timeee_1_increment), .D0(current_time[12]), .D1(current_time[13]),
    .D2(current_time[14]), .D3(current_time[15]), .cout(counter05_2_cout));
  counter24h counter24h_1 (
    .Enable(counter05_2_cout), .Reset(Reset), .CLK(glitch_free_mux_v2_1_clk_out),
    .increment(setting_timeee_1_increment), .D0(current_time[16]), .D1(current_time[17]),
    .D2(current_time[18]), .D3(current_time[19]), .D4(current_time[20]), .Cout(counter24h_1_cout));
  // NoConnect on counter24h_1_cout
  counter09 counter09_1 (
    .Enable(ENable_gate_out), .CLK(glitch_free_mux_v2_1_clk_out), .Reset(Reset),
    .increment(setting_timeee_1_increment), .D0(current_time[0]), .D1(current_time[1]), .D2(current_time[2]),
    .D3(current_time[3]), .cout(counter09_1_cout));
  counter05 counter05_1 (
    .Enable(counter09_1_cout), .CLK(glitch_free_mux_v2_1_clk_out), .Reset(Reset),
    .increment(setting_timeee_1_increment), .D0(current_time[4]), .D1(current_time[5]), .D2(current_time[6]),
    .D3(current_time[7]), .cout(counter05_1_cout));
  seven_segment_display_decoder seven_segment_display_decoder_3 (
    .w(current_time[8]), .x(current_time[9]), .y(current_time[10]), .z(current_time[11]), .a(MinLSD[0]),
    .b(MinLSD[1]), .c(MinLSD[2]), .d(MinLSD[3]), .e(MinLSD[4]), .f(MinLSD[5]), .g(MinLSD[6]));
  seven_segment_display_decoder seven_segment_display_decoder_4 (
    .w(current_time[12]), .x(current_time[13]), .y(current_time[14]), .z(current_time[15]), .a(MINs_MSD[0]),
    .b(MINs_MSD[1]), .c(MINs_MSD[2]), .d(MINs_MSD[3]), .e(MINs_MSD[4]), .f(MINs_MSD[5]), .g(MINs_MSD[6]));
  decoder24h_to_display decoder24h_to_display_1 (
    .v(current_time[16]), .w(current_time[17]), .x(current_time[18]), .y(current_time[19]),
    .z(current_time[20]), .a1(HOURS_MSD[0]), .b1(HOURS_MSD[1]), .c1(HOURS_MSD[2]), .d1(HOURS_MSD[3]),
    .e1(HOURS_MSD[4]), .f1(HOURS_MSD[5]), .g1(HOURS_MSD[6]), .a0(HOUR_LSD[0]), .b0(HOUR_LSD[1]),
    .c0(HOUR_LSD[2]), .d0(HOUR_LSD[3]), .e0(HOUR_LSD[4]), .f0(HOUR_LSD[5]), .g0(HOUR_LSD[6]));
  seven_segment_display_decoder seven_segment_display_decoder_1 (
    .w(current_time[0]), .x(current_time[1]), .y(current_time[2]), .z(current_time[3]), .a(secondsLSD[0]),
    .b(secondsLSD[1]), .c(secondsLSD[2]), .d(secondsLSD[3]), .e(secondsLSD[4]), .f(secondsLSD[5]),
    .g(secondsLSD[6]));
  seven_segment_display_decoder seven_segment_display_decoder_2 (
    .w(current_time[4]), .x(current_time[5]), .y(current_time[6]), .z(current_time[7]), .a(Seconds_MSD[0]),
    .b(Seconds_MSD[1]), .c(Seconds_MSD[2]), .d(Seconds_MSD[3]), .e(Seconds_MSD[4]), .f(Seconds_MSD[5]),
    .g(Seconds_MSD[6]));

  // Other names for the same wires on the sheet: seconds_LSD[3:0] = current_time[3:0];
  //   seconds_MSD_t[3:0] = current_time[7:4]; mins_LSD[3:0] = current_time[11:8];
  //   mins_MSD_t[3:0] = current_time[15:12]; hours[4:0] = current_time[20:16]

  // Notes on the sheet:
  //   there are variations of that on the internet 
  //   it was validated by un assistant
  //   this is glitch free explanation in report
  //   (famous glitch free Mux fpr clocks) 
  //   increment-> logic 1
  //   decrement ->logic0
  //   5 bits
  //   4 bits
  //   4 bits
  //   4 bits
  //   4 bits
  //   Minutes LSd
  //   Minutes MSD
  //   SECONDS MSd
  //   seconds LSdigit
  //   Hours MSB
  //   hours LSB
endmodule

// 0-5 counter
module counter05 (
  input  Enable,
  input  CLK,
  input  Reset,
  input  increment,
  output D0,
  output D1,
  output D2,
  output D3,
  output cout
);

  wire d_ff_1_qn, d_ff_2_qn, d_ff_3_qn, d_ff_4_qn, transition_logic_05_1_d0, transition_logic_05_1_d1,
       transition_logic_05_1_d2, transition_logic_05_1_d3;

  transition_logic_05 transition_logic_05_1 (
    .C0(D0), .C1(D1), .C2(D2), .C3(D3), .Enable(Enable), .Increment(increment),
    .D0(transition_logic_05_1_d0), .D1(transition_logic_05_1_d1), .D2(transition_logic_05_1_d2),
    .D3(transition_logic_05_1_d3), .Cout(cout));
  D_Flip_Flop d_ff_1 (.D(transition_logic_05_1_d0), .clk(CLK), .Q(D0), .Qn(d_ff_1_qn), .reset(Reset));  // open: preset
  D_Flip_Flop d_ff_2 (.D(transition_logic_05_1_d1), .clk(CLK), .Q(D1), .Qn(d_ff_2_qn), .reset(Reset));  // open: preset
  D_Flip_Flop d_ff_3 (.D(transition_logic_05_1_d2), .clk(CLK), .Q(D2), .Qn(d_ff_3_qn), .reset(Reset));  // open: preset
  D_Flip_Flop d_ff_4 (.D(transition_logic_05_1_d3), .clk(CLK), .Q(D3), .Qn(d_ff_4_qn), .reset(Reset));  // open: preset
  // NoConnect on d_ff_1_qn
  // NoConnect on d_ff_2_qn
  // NoConnect on d_ff_3_qn
  // NoConnect on d_ff_4_qn
endmodule

module transition_logic_05 (
  input  C0,
  input  C1,
  input  C2,
  input  C3,
  input  Enable,
  input  Increment,
  output D0,
  output D1,
  output D2,
  output D3,
  output Cout
);

  wire and_1_out, and_2_out, and_3_out, and_4_out, and_5_out, and_6_out, and_7_out, and_8_out, and_9_out,
       and_10_out, and_11_out, and_12_out, and_13_out, and_14_out, and_15_out, and_16_out, and_17_out,
       and_18_out, and_19_out, not_1_out, not_2_out, not_3_out, not_4_out, not_5_out, not_6_out;

  not not_1 (not_1_out, C0);
  not not_2 (not_2_out, C1);
  not not_3 (not_3_out, C2);
  not not_4 (not_4_out, C3);
  not not_5 (not_5_out, Enable);
  not not_6 (not_6_out, Increment);
  and and_1 (and_1_out, Increment, C2, C3, Enable);
  and and_2 (and_2_out, Increment, C1, not_4_out);
  and and_3 (and_3_out, C1, not_5_out);
  and and_4 (and_4_out, not_6_out, not_1_out, not_2_out, not_3_out, not_4_out, Enable);
  and and_5 (and_5_out, not_6_out, not_1_out, C1, C3);
  and and_6 (and_6_out, C1, C2);
  and and_7 (and_7_out, C0, C2, C3, Enable);
  and and_8 (and_8_out, C0, C1, not_4_out);
  and and_9 (and_9_out, Increment, not_2_out, not_3_out, C3, Enable);
  and and_10 (and_10_out, Increment, C2, not_4_out);
  and and_11 (and_11_out, C2, not_5_out);
  and and_12 (and_12_out, not_6_out, not_1_out, not_2_out, C2, C3);
  and and_13 (and_13_out, not_6_out, not_1_out, C1, not_4_out, Enable);
  and and_14 (and_14_out, C0, not_2_out, not_3_out, C3, Enable);
  and and_15 (and_15_out, C0, C2, not_4_out);
  and and_16 (and_16_out, not_5_out, C3);
  and and_17 (and_17_out, Enable, not_4_out);
  and and_18 (and_18_out, not_6_out, not_1_out, not_2_out, not_3_out, not_4_out, Enable);
  and and_19 (and_19_out, Increment, not_1_out, C1, not_3_out, C3, Enable);
  or or_1 (D2, and_9_out, and_10_out, and_11_out, and_12_out, and_13_out, and_14_out, and_15_out);
  or or_2 (D3, and_16_out, and_17_out);
  or or_3 (Cout, and_18_out, and_19_out);
  or or_4 (D1, and_1_out, and_2_out, and_3_out, and_4_out, and_5_out, and_6_out, and_7_out, and_8_out);

  assign D0 = 1'b0;
endmodule

module counter24h (
  input  Enable,
  input  Reset,
  input  CLK,
  input  increment,
  output D0,
  output D1,
  output D2,
  output D3,
  output D4,
  output Cout
);

  wire d_ff_1_qn, d_ff_2_qn, d_ff_3_qn, d_ff_4_qn, d_ff_5_qn, full_transition_logic_24h_1_d0,
       full_transition_logic_24h_1_d1, full_transition_logic_24h_1_d2, full_transition_logic_24h_1_d3,
       full_transition_logic_24h_1_d4;

  full_transition_logic_24h full_transition_logic_24h_1 (
    .C0(D0), .C1(D1), .C2(D2), .C3(D3), .C4(D4), .Enable(Enable), .increment(increment),
    .D0(full_transition_logic_24h_1_d0), .D1(full_transition_logic_24h_1_d1),
    .D2(full_transition_logic_24h_1_d2), .D3(full_transition_logic_24h_1_d3),
    .D4(full_transition_logic_24h_1_d4), .cout(Cout));
  D_Flip_Flop d_ff_1 (
    .D(full_transition_logic_24h_1_d0), .clk(CLK), .Q(D0), .Qn(d_ff_1_qn), .reset(Reset));  // open: preset
  D_Flip_Flop d_ff_2 (
    .D(full_transition_logic_24h_1_d1), .clk(CLK), .Q(D1), .Qn(d_ff_2_qn), .reset(Reset));  // open: preset
  D_Flip_Flop d_ff_3 (
    .D(full_transition_logic_24h_1_d2), .clk(CLK), .Q(D2), .Qn(d_ff_3_qn), .reset(Reset));  // open: preset
  D_Flip_Flop d_ff_4 (
    .D(full_transition_logic_24h_1_d3), .clk(CLK), .Q(D3), .Qn(d_ff_4_qn), .reset(Reset));  // open: preset
  D_Flip_Flop d_ff_5 (
    .D(full_transition_logic_24h_1_d4), .clk(CLK), .Q(D4), .Qn(d_ff_5_qn), .reset(Reset));  // open: preset
  // NoConnect on d_ff_1_qn
  // NoConnect on d_ff_2_qn
  // NoConnect on d_ff_3_qn
  // NoConnect on d_ff_4_qn
  // NoConnect on d_ff_5_qn
endmodule

// increment 24h
module transition_logic24h_increment (
  input  C0,
  input  C1,
  input  C2,
  input  C3,
  input  C4,
  input  Enable,
  output D0,
  output D1,
  output D2,
  output D3,
  output D4,
  output Cout
);

  wire and_1_out, and_2_out, and_3_out, and_4_out, and_5_out, and_6_out, and_7_out, and_8_out, and_9_out,
       and_10_out, and_11_out, and_12_out, and_13_out, and_14_out, and_15_out, and_16_out, and_17_out,
       and_18_out, and_19_out, not_1_out, not_2_out, not_3_out, not_4_out, not_5_out, not_6_out;

  not not_1 (not_1_out, C0);
  not not_2 (not_2_out, C1);
  not not_3 (not_3_out, C2);
  not not_4 (not_4_out, C3);
  not not_5 (not_5_out, C4);
  not not_6 (not_6_out, Enable);
  and and_1 (and_1_out, C0, not_3_out);
  and and_2 (and_2_out, C0, not_4_out);
  and and_3 (and_3_out, C0, not_5_out);
  and and_4 (and_4_out, C0, not_6_out);
  and and_5 (and_5_out, C1, C2, C3, C4, Enable);
  and and_6 (and_6_out, not_1_out, not_2_out, C2, C3, C4, Enable);
  and and_7 (and_7_out, C1, not_3_out);
  and and_8 (and_8_out, C1, not_4_out);
  and and_9 (and_9_out, C1, not_5_out);
  and and_10 (and_10_out, C1, not_6_out);
  and and_11 (and_11_out, not_3_out, C3, C4, Enable);
  and and_12 (and_12_out, C2, not_4_out);
  and and_13 (and_13_out, C2, not_5_out);
  and and_14 (and_14_out, C2, not_6_out);
  and and_15 (and_15_out, not_4_out, C4, Enable);
  and and_16 (and_16_out, C3, not_5_out);
  and and_17 (and_17_out, C3, not_6_out);
  and and_18 (and_18_out, not_5_out, Enable);
  and and_19 (and_19_out, C4, not_6_out);
  and and_20 (Cout, C0, C2, C3, C4, Enable);
  or or_1 (D0, and_1_out, and_2_out, and_3_out, and_4_out, and_5_out);
  or or_2 (D1, and_6_out, and_7_out, and_8_out, and_9_out, and_10_out);
  or or_3 (D2, and_11_out, and_12_out, and_13_out, and_14_out);
  or or_4 (D3, and_15_out, and_16_out, and_17_out);
  or or_5 (D4, and_18_out, and_19_out);
endmodule

// display_decoder24h
module decoder24h_to_display (
  input  v,
  input  w,
  input  x,
  input  y,
  input  z,
  output a1,
  output b1,
  output c1,
  output d1,
  output e1,
  output f1,
  output g1,
  output a0,
  output b0,
  output c0,
  output d0,
  output e0,
  output f0,
  output g0
);

  wire and_1_out, and_2_out, and_3_out, and_4_out, and_5_out, and_6_out, and_7_out, and_8_out, and_9_out,
       and_10_out, and_11_out, and_13_out, and_14_out, and_15_out, and_16_out, and_17_out, and_18_out,
       and_19_out, and_20_out, and_21_out, and_22_out, and_23_out, and_24_out, and_25_out, and_26_out,
       and_27_out, and_28_out, and_29_out, and_30_out, and_31_out, and_32_out, and_33_out, and_34_out,
       and_35_out, and_36_out, and_37_out, and_38_out, and_39_out, and_40_out, and_41_out, and_42_out,
       and_43_out, and_44_out, and_45_out, and_46_out, and_47_out, and_48_out, and_49_out, and_50_out,
       and_51_out, and_52_out, and_53_out, and_54_out, and_55_out, not_1_out, not_2_out, not_3_out,
       not_4_out, not_5_out;

  not not_1 (not_1_out, v);
  not not_2 (not_2_out, w);
  not not_3 (not_3_out, x);
  not not_4 (not_4_out, y);
  not not_5 (not_5_out, z);
  and and_1 (and_1_out, not_1_out, not_3_out, not_4_out);
  and and_2 (and_2_out, not_2_out, x);
  and and_3 (and_3_out, not_1_out, not_2_out);
  or or_1 (c1, not_3_out, not_1_out);
  and and_4 (and_4_out, not_1_out, not_3_out, not_4_out);
  and and_5 (and_5_out, not_2_out, x);
  and and_6 (and_6_out, not_1_out, not_2_out);
  and and_7 (and_7_out, not_1_out, not_3_out, not_4_out);
  and and_8 (and_8_out, not_2_out, x);
  and and_9 (and_9_out, not_1_out, not_2_out);
  and and_10 (and_10_out, not_1_out, not_2_out);
  and and_11 (and_11_out, not_1_out, not_3_out, not_4_out);
  and and_12 (g1, v, x);
  and and_13 (and_13_out, not_3_out, not_5_out);
  and and_14 (and_14_out, not_2_out, y);
  and and_15 (and_15_out, not_1_out, x, z);
  and and_16 (and_16_out, w, not_4_out);
  and and_17 (and_17_out, v, not_3_out);
  and and_18 (and_18_out, v, not_5_out);
  and and_19 (and_19_out, not_2_out, y, z);
  and and_20 (and_20_out, w, not_4_out);
  and and_21 (and_21_out, w, not_5_out);
  and and_22 (and_22_out, not_1_out, not_3_out);
  and and_23 (and_23_out, x, not_4_out, not_5_out);
  and and_24 (and_24_out, v, z);
  and and_25 (and_25_out, v, y);
  and and_26 (and_26_out, v, not_3_out);
  and and_27 (and_27_out, not_2_out, not_4_out);
  and and_28 (and_28_out, not_1_out, x, y);
  and and_29 (and_29_out, w, not_3_out);
  and and_30 (and_30_out, not_3_out, not_5_out);
  and and_31 (and_31_out, not_2_out, not_3_out, y);
  and and_32 (and_32_out, not_1_out, x, not_4_out, z);
  and and_33 (and_33_out, not_2_out, y, not_5_out);
  and and_34 (and_34_out, w, not_4_out);
  and and_35 (and_35_out, w, x, z);
  and and_36 (and_36_out, v, not_5_out);
  and and_37 (and_37_out, v, y);
  and and_38 (and_38_out, not_3_out, not_5_out);
  and and_39 (and_39_out, v, not_5_out);
  and and_40 (and_40_out, not_2_out, y, not_5_out);
  and and_41 (and_41_out, w, not_4_out, not_5_out);
  and and_42 (and_42_out, v, not_3_out, y);
  and and_43 (and_43_out, not_1_out, not_2_out, x, not_4_out);
  and and_44 (and_44_out, w, not_3_out, not_4_out);
  and and_45 (and_45_out, w, x, y);
  and and_46 (and_46_out, not_2_out, not_4_out, not_5_out);
  and and_47 (and_47_out, w, not_3_out, not_5_out);
  and and_48 (and_48_out, not_1_out, x, y, not_5_out);
  and and_49 (and_49_out, not_2_out, not_3_out, y);
  and and_50 (and_50_out, not_1_out, x, not_4_out);
  and and_51 (and_51_out, w, not_4_out);
  and and_52 (and_52_out, w, x);
  and and_53 (and_53_out, v, not_3_out, not_5_out);
  and and_54 (and_54_out, v, y);
  and and_55 (and_55_out, not_2_out, y, not_5_out);
  or or_2 (a1, and_1_out, and_2_out, and_3_out);
  or or_3 (d1, and_4_out, and_5_out, and_6_out);
  or or_4 (e1, and_7_out, and_8_out, and_9_out);
  or or_5 (f1, and_10_out, and_11_out);
  or or_6 (a0, and_13_out, and_14_out, and_15_out, and_16_out, and_17_out, and_18_out);
  or or_7 (b0, and_19_out, and_20_out, and_21_out, and_22_out, and_23_out, and_24_out, and_25_out);
  or or_8 (c0, z, and_26_out, and_27_out, and_28_out, and_29_out);
  or or_9 (d0, and_30_out, and_31_out, and_32_out, and_33_out, and_34_out, and_35_out, and_36_out, and_37_out);
  or or_10 (e0, and_38_out, and_39_out, and_40_out, and_41_out);
  or or_11 (f0, and_42_out, and_43_out, and_44_out, and_45_out, and_46_out, and_47_out, and_48_out);
  or or_12 (g0, and_49_out, and_50_out, and_51_out, and_52_out, and_53_out, and_54_out, and_55_out);

  assign b1 = 1'b1;
endmodule

module ENcoder_rotational_butt (
  input  CHB0,
  input  CHA0,
  input  CHB1,
  input  CHA1,
  input  E,
  output dir,
  output cnt_en
);

  wire and_1_out, and_2_out, and_3_out, and_4_out, and_5_out, and_6_out, and_7_out, and_8_out, and_9_out,
       and_10_out, not_1_out, not_2_out, not_3_out, not_4_out;

  not not_1 (not_1_out, CHB0);
  not not_2 (not_2_out, CHA0);
  not not_3 (not_3_out, CHB1);
  not not_4 (not_4_out, CHA1);
  and and_1 (and_1_out, CHB0, not_4_out);
  and and_2 (and_2_out, not_1_out, CHA1);
  and and_3 (and_3_out, CHB0, not_2_out, not_3_out, not_4_out, E);
  and and_4 (and_4_out, not_1_out, not_2_out, not_3_out, CHA1, E);
  and and_5 (and_5_out, not_1_out, not_2_out, CHB1, not_4_out, E);
  and and_6 (and_6_out, CHB0, not_2_out, CHB1, CHA1, E);
  and and_7 (and_7_out, not_1_out, CHA0, not_3_out, not_4_out, E);
  and and_8 (and_8_out, CHB0, CHA0, not_3_out, CHA1, E);
  and and_9 (and_9_out, CHB0, CHA0, CHB1, not_4_out, E);
  and and_10 (and_10_out, not_1_out, CHA0, CHB1, CHA1, E);
  or or_1 (dir, and_1_out, and_2_out);
  or or_2 (cnt_en, and_3_out, and_4_out, and_5_out, and_6_out, and_7_out, and_8_out, and_9_out, and_10_out);
endmodule

// filtre
module bouncing_filter (
  input  INPUT_SIGNAL,
  input  CLK,
  input  RESET,
  output SIGNAL_OUT
);

  wire d_ff_1_q, d_ff_1_qn, d_ff_2_q, d_ff_2_qn, d_ff_3_q, d_ff_3_qn, d_ff_4_q, d_ff_4_qn;

  D_Flip_Flop d_ff_1 (.D(INPUT_SIGNAL), .clk(CLK), .Q(d_ff_1_q), .Qn(d_ff_1_qn), .reset(RESET));  // open: preset
  // NoConnect on d_ff_1_qn
  D_Flip_Flop d_ff_2 (.D(d_ff_1_q), .clk(CLK), .Q(d_ff_2_q), .Qn(d_ff_2_qn), .reset(RESET));  // open: preset
  D_Flip_Flop d_ff_3 (.D(d_ff_2_q), .clk(CLK), .Q(d_ff_3_q), .Qn(d_ff_3_qn), .reset(RESET));  // open: preset
  // NoConnect on d_ff_3_qn
  D_Flip_Flop d_ff_4 (.D(d_ff_3_q), .clk(CLK), .Q(d_ff_4_q), .Qn(d_ff_4_qn), .reset(RESET));  // open: preset
  // NoConnect on d_ff_4_qn
  // NoConnect on d_ff_2_qn
  and and_1 (SIGNAL_OUT, d_ff_1_q, d_ff_2_q, d_ff_3_q, d_ff_4_q);
endmodule

module Decoder_Rotation (
  input  CHA,
  input  CHB,
  input  CLK,
  input  Reset,
  output CCW,
  output CW
);

  wire and_1_out, and_2_out, and_3_out, and_4_out, bouncing_filter_1_signal_out,
       bouncing_filter_2_signal_out, d_ff_1_q, d_ff_1_qn, d_ff_2_q, d_ff_2_qn, d_ff_3_q, d_ff_3_qn, d_ff_4_q,
       d_ff_4_qn;

  D_Flip_Flop d_ff_1 (
    .D(bouncing_filter_1_signal_out), .clk(CLK), .Q(d_ff_1_q), .Qn(d_ff_1_qn), .reset(Reset));  // open: preset
  bouncing_filter bouncing_filter_1 (
    .INPUT_SIGNAL(CHA), .CLK(CLK), .RESET(Reset), .SIGNAL_OUT(bouncing_filter_1_signal_out));
  D_Flip_Flop d_ff_2 (
    .D(bouncing_filter_2_signal_out), .clk(CLK), .Q(d_ff_2_q), .Qn(d_ff_2_qn), .reset(Reset));  // open: preset
  bouncing_filter bouncing_filter_2 (
    .INPUT_SIGNAL(CHB), .CLK(CLK), .RESET(Reset), .SIGNAL_OUT(bouncing_filter_2_signal_out));
  D_Flip_Flop d_ff_3 (.D(d_ff_1_q), .clk(CLK), .Q(d_ff_3_q), .Qn(d_ff_3_qn), .reset(Reset));  // open: preset
  D_Flip_Flop d_ff_4 (.D(d_ff_2_q), .clk(CLK), .Q(d_ff_4_q), .Qn(d_ff_4_qn), .reset(Reset));  // open: preset
  and and_1 (and_1_out, d_ff_1_q, d_ff_3_q, d_ff_2_qn, d_ff_4_q);
  and and_2 (and_2_out, d_ff_4_q, d_ff_1_q, d_ff_2_q, d_ff_3_qn);
  and and_3 (and_3_out, d_ff_1_qn, d_ff_2_q, d_ff_3_q, d_ff_4_q);
  and and_4 (and_4_out, d_ff_1_q, d_ff_2_q, d_ff_3_q, d_ff_4_qn);
  or or_1 (CCW, and_1_out, and_2_out);
  or or_2 (CW, and_3_out, and_4_out);
endmodule

module testing_rotation (
  input  CHA_PIN4,
  input  CHB_PIN5,
  input  Reset,
  input  CH_C,
  output Vcc,
  output GND
);

  wire bouncing_filter_1_signal_out, clock_1_out, clock_2_out, Decoder_Rotation_1_ccw, Decoder_Rotation_1_cw,
       not_1_out, toggle_button_1_outputtt;

  Clock clock_1 (.out(clock_1_out));
  not not_1 (not_1_out, CH_C);
  Clock clock_2 (.out(clock_2_out));
  bouncing_filter bouncing_filter_1 (
    .INPUT_SIGNAL(not_1_out), .CLK(clock_1_out), .RESET(Reset), .SIGNAL_OUT(bouncing_filter_1_signal_out));
  Decoder_Rotation Decoder_Rotation_1 (
    .CHA(CHA_PIN4), .CHB(CHB_PIN5), .CLK(clock_2_out), .Reset(Reset), .CCW(Decoder_Rotation_1_ccw),
    .CW(Decoder_Rotation_1_cw));
  _7_Segment_Display CW_display (
    .g(Decoder_Rotation_1_ccw), .f(Decoder_Rotation_1_ccw), .a(Decoder_Rotation_1_ccw),
    .b(Decoder_Rotation_1_ccw), .e(Decoder_Rotation_1_ccw), .d(Decoder_Rotation_1_ccw),
    .c(Decoder_Rotation_1_ccw), .dp(Decoder_Rotation_1_ccw));
  _7_Segment_Display L_7_Segment_Display_1 (
    .g(Decoder_Rotation_1_cw), .f(Decoder_Rotation_1_cw), .a(Decoder_Rotation_1_cw),
    .b(Decoder_Rotation_1_cw), .e(Decoder_Rotation_1_cw), .d(Decoder_Rotation_1_cw),
    .c(Decoder_Rotation_1_cw), .dp(Decoder_Rotation_1_cw));
  toggle_button toggle_button_1 (
    .Buttonn(bouncing_filter_1_signal_out), .CLK(clock_1_out), .Reset(Reset),
    .outputtt(toggle_button_1_outputtt));
  _7_Segment_Display C_PRESS (
    .g(toggle_button_1_outputtt), .f(toggle_button_1_outputtt), .a(toggle_button_1_outputtt),
    .b(toggle_button_1_outputtt), .e(toggle_button_1_outputtt), .d(toggle_button_1_outputtt),
    .c(toggle_button_1_outputtt), .dp(toggle_button_1_outputtt));

  assign GND = 1'b0;
  assign Vcc = 1'b1;

  // Notes on the sheet:
  //   Pression verticale
  //   the CH_C button is weirdddddddddddd it son by defsult for some weird reason
endmodule

module full_transition_logic_24h (
  input  C0,
  input  C1,
  input  C2,
  input  C3,
  input  C4,
  input  Enable,
  input  increment,
  output D0,
  output D1,
  output D2,
  output D3,
  output D4,
  output cout
);

  wire demultiplexer_1_out0, demultiplexer_1_out1, transition_logic24h_decrement_1_cout,
       transition_logic24h_decrement_1_d0, transition_logic24h_decrement_1_d1,
       transition_logic24h_decrement_1_d2, transition_logic24h_decrement_1_d3,
       transition_logic24h_decrement_1_d4, transition_logic24h_increment_1_cout,
       transition_logic24h_increment_1_d0, transition_logic24h_increment_1_d1,
       transition_logic24h_increment_1_d2, transition_logic24h_increment_1_d3,
       transition_logic24h_increment_1_d4;

  Demultiplexer #(.enable("true")) demultiplexer_1 (
    .out0(demultiplexer_1_out0), .out1(demultiplexer_1_out1), .in(Enable), .sel(increment), .en(1'b1));
  transition_logic24h_increment transition_logic24h_increment_1 (
    .C0(C0), .C1(C1), .C2(C2), .C3(C3), .C4(C4), .Enable(demultiplexer_1_out1),
    .D0(transition_logic24h_increment_1_d0), .D1(transition_logic24h_increment_1_d1),
    .D2(transition_logic24h_increment_1_d2), .D3(transition_logic24h_increment_1_d3),
    .D4(transition_logic24h_increment_1_d4), .Cout(transition_logic24h_increment_1_cout));
  transition_logic24h_decrement transition_logic24h_decrement_1 (
    .Enable(demultiplexer_1_out0), .C0(C0), .C1(C1), .C2(C2), .C3(C3), .C4(C4),
    .D0(transition_logic24h_decrement_1_d0), .D1(transition_logic24h_decrement_1_d1),
    .D2(transition_logic24h_decrement_1_d2), .D3(transition_logic24h_decrement_1_d3),
    .D4(transition_logic24h_decrement_1_d4), .Cout(transition_logic24h_decrement_1_cout));
  Multiplexer multiplexer_1 (
    .in0(transition_logic24h_decrement_1_d0), .in1(transition_logic24h_increment_1_d0), .out(D0),
    .sel(increment));
  Multiplexer multiplexer_2 (
    .in0(transition_logic24h_decrement_1_d1), .in1(transition_logic24h_increment_1_d1), .out(D1),
    .sel(increment));
  Multiplexer multiplexer_3 (
    .in0(transition_logic24h_decrement_1_d2), .in1(transition_logic24h_increment_1_d2), .out(D2),
    .sel(increment));
  Multiplexer multiplexer_4 (
    .in0(transition_logic24h_decrement_1_d3), .in1(transition_logic24h_increment_1_d3), .out(D3),
    .sel(increment));
  Multiplexer multiplexer_5 (
    .in0(transition_logic24h_decrement_1_d4), .in1(transition_logic24h_increment_1_d4), .out(D4),
    .sel(increment));
  Multiplexer multiplexer_6 (
    .in0(transition_logic24h_decrement_1_cout), .in1(transition_logic24h_increment_1_cout), .out(cout),
    .sel(increment));

  // Notes on the sheet:
  //   PAS SYMPAS L'HISTOIRE DU 1 LA
endmodule

// deccrement 24h
module transition_logic24h_decrement (
  input  Enable,
  input  C0,
  input  C1,
  input  C2,
  input  C3,
  input  C4,
  output D0,
  output D1,
  output D2,
  output D3,
  output D4,
  output Cout
);

  wire and_1_out, and_2_out, and_3_out, and_4_out, and_5_out, and_6_out, and_7_out, and_8_out, and_9_out,
       and_10_out, and_11_out, and_12_out, and_13_out, and_14_out, and_15_out, and_16_out, and_17_out,
       and_18_out, and_19_out, not_1_out, not_2_out, not_3_out, not_4_out, not_5_out, not_6_out;

  not not_1 (not_1_out, Enable);
  not not_2 (not_2_out, C0);
  not not_3 (not_3_out, C1);
  not not_4 (not_4_out, C2);
  not not_5 (not_5_out, C3);
  not not_6 (not_6_out, C4);
  and and_1 (and_1_out, not_1_out, C0);
  and and_2 (and_2_out, Enable, not_2_out, not_3_out, not_4_out, not_5_out, not_6_out);
  and and_3 (and_3_out, C0, C4);
  and and_4 (and_4_out, C0, C3);
  and and_5 (and_5_out, C0, C2);
  and and_6 (and_6_out, not_1_out, C1);
  and and_7 (and_7_out, C1, C4);
  and and_8 (and_8_out, C1, C3);
  and and_9 (and_9_out, C1, C2);
  and and_10 (and_10_out, Enable, C0, not_4_out, not_5_out, not_6_out);
  and and_11 (and_11_out, Enable, not_4_out, not_5_out, not_6_out);
  and and_12 (and_12_out, not_1_out, C2);
  and and_13 (and_13_out, C2, C4);
  and and_14 (and_14_out, C2, C3);
  and and_15 (and_15_out, Enable, not_5_out, not_6_out);
  and and_16 (and_16_out, not_1_out, C3);
  and and_17 (and_17_out, C3, C4);
  and and_18 (and_18_out, Enable, not_6_out);
  and and_19 (and_19_out, not_1_out, C4);
  and and_20 (Cout, Enable, not_2_out, not_3_out, not_4_out, not_5_out, not_6_out);
  or or_1 (D0, and_1_out, and_2_out, and_3_out, and_4_out, and_5_out);
  or or_2 (D1, and_6_out, and_7_out, and_8_out, and_9_out, and_10_out);
  or or_3 (D2, and_11_out, and_12_out, and_13_out, and_14_out);
  or or_4 (D3, and_15_out, and_16_out, and_17_out);
  or or_5 (D4, and_18_out, and_19_out);
endmodule

module state_selector_Decder (
  input  D2,
  input  D1,
  input  D0,
  output Time_setting,
  output State1,
  output State2,
  output State3,
  output State4,
  output State5,
  output state6,
  output State7
);

  wire not_1_out, not_2_out, not_3_out;

  not not_1 (not_1_out, D2);
  not not_2 (not_2_out, D1);
  not not_3 (not_3_out, D0);
  and and_1 (Time_setting, not_1_out, not_2_out, not_3_out);
  and and_2 (State1, not_1_out, not_2_out, D0);
  and and_3 (State2, not_1_out, D1, not_3_out);
  and and_4 (State3, not_1_out, D1, D0);
  and and_5 (State4, D2, not_2_out, not_3_out);
  and and_6 (State5, D2, not_2_out, D0);
  and and_7 (state6, D2, D1, not_3_out);
  and and_8 (State7, D2, D1, D0);
endmodule

module toggle_button (
  input  Buttonn,
  input  CLK,
  input  Reset,
  output outputtt
);

  wire rising_edge_detector_1_outttt, t_ff_1_qn;

  rising_edge_detector rising_edge_detector_1 (
    .inputt(Buttonn), .CLk(CLK), .Reset(Reset), .outttt(rising_edge_detector_1_outttt));
  T_Flip_Flop t_ff_1 (
    .T(rising_edge_detector_1_outttt), .clk(CLK), .Q(outputtt), .Qn(t_ff_1_qn), .reset(Reset));  // open: preset
  // NoConnect on t_ff_1_qn
endmodule

module rising_edge_detector (
  input  inputt,
  input  CLk,
  input  Reset,
  output outttt
);

  wire d_ff_1_q, d_ff_1_qn;

  D_Flip_Flop d_ff_1 (.D(inputt), .clk(CLk), .Q(d_ff_1_q), .Qn(d_ff_1_qn), .reset(Reset));  // open: preset
  // NoConnect on d_ff_1_q
  and and_1 (outttt, inputt, d_ff_1_qn);

  // Notes on the sheet:
  //   rising edge detector
endmodule

module state_selector_FSM (
  input  inputtttttttttt,
  input  CLk,
  input  Reset,
  output D2,
  output D1,
  output D0
);

  wire d_ff_1_qn, d_ff_2_qn, d_ff_3_qn, trans_logic_state_delector_toggle_1_d0,
       trans_logic_state_delector_toggle_1_d1, trans_logic_state_delector_toggle_1_d2;

  Transition_logic_state_selector trans_logic_state_delector_toggle_1 (
    .C2(D2), .C1(D1), .C0(D0), .Button(inputtttttttttt), .D2(trans_logic_state_delector_toggle_1_d2),
    .D1(trans_logic_state_delector_toggle_1_d1), .D0(trans_logic_state_delector_toggle_1_d0));
  D_Flip_Flop d_ff_1 (
    .D(trans_logic_state_delector_toggle_1_d2), .clk(CLk), .Q(D2), .Qn(d_ff_1_qn), .reset(Reset));  // open: preset
  // NoConnect on d_ff_1_qn
  D_Flip_Flop d_ff_2 (
    .D(trans_logic_state_delector_toggle_1_d1), .clk(CLk), .Q(D1), .Qn(d_ff_2_qn), .reset(Reset));  // open: preset
  // NoConnect on d_ff_2_qn
  D_Flip_Flop d_ff_3 (
    .D(trans_logic_state_delector_toggle_1_d0), .clk(CLk), .Q(D0), .Qn(d_ff_3_qn), .reset(Reset));  // open: preset
  // NoConnect on d_ff_3_qn
endmodule

module Transition_logic_state_selector (
  input  C2,
  input  C1,
  input  C0,
  input  Button,
  output D2,
  output D1,
  output D0
);

  wire and_1_out, and_2_out, and_3_out, and_4_out, and_5_out, and_6_out, and_7_out, not_1_out, not_2_out,
       not_3_out, not_4_out;

  not not_1 (not_1_out, C2);
  not not_2 (not_2_out, C1);
  not not_3 (not_3_out, C0);
  not not_4 (not_4_out, Button);
  and and_1 (and_1_out, not_1_out, C1, C0, not_4_out);
  and and_2 (and_2_out, C2, not_2_out);
  and and_3 (and_3_out, C2, not_3_out);
  and and_4 (and_4_out, C2, Button);
  and and_5 (and_5_out, not_2_out, C0, not_4_out);
  and and_6 (and_6_out, C1, not_3_out);
  and and_7 (and_7_out, C1, Button);
  or or_1 (D2, and_1_out, and_2_out, and_3_out, and_4_out);
  or or_2 (D1, and_5_out, and_6_out, and_7_out);

  assign D0 = Button;
endmodule

// STOP WATCH
module stop_watch (
  input  START1_STOP0,
  input  Reset,
  input  FASTEST_CLK,
  input  State2,
  output [6:0] display0gfedcba,
  output [6:0] display1gfedcba,
  output [6:0] display2gfedcba,
  output [6:0] display3gfedcba,
  output [6:0] display4gfedcba,
  output [6:0] display5gfedcba
);

  wire and_1_out, counter05_1_cout, counter05_1_d0, counter05_1_d1, counter05_1_d2, counter05_1_d3,
       counter05_2_cout, counter05_2_d0, counter05_2_d1, counter05_2_d2, counter05_2_d3, counter09_1_cout,
       counter09_1_d0, counter09_1_d1, counter09_1_d2, counter09_1_d3, counter09_2_cout, counter09_2_d0,
       counter09_2_d1, counter09_2_d2, counter09_2_d3, counter09_3_cout, counter09_3_d0, counter09_3_d1,
       counter09_3_d2, counter09_3_d3, counter09_4_cout, counter09_4_d0, counter09_4_d1, counter09_4_d2,
       counter09_4_d3;

  and and_1 (and_1_out, START1_STOP0, State2);
  counter09 counter09_1 (
    .Enable(and_1_out), .CLK(FASTEST_CLK), .Reset(Reset), .increment(1'b1), .D0(counter09_1_d0),
    .D1(counter09_1_d1), .D2(counter09_1_d2), .D3(counter09_1_d3), .cout(counter09_1_cout));
  counter09 counter09_2 (
    .Enable(counter09_1_cout), .CLK(FASTEST_CLK), .Reset(Reset), .increment(1'b1), .D0(counter09_2_d0),
    .D1(counter09_2_d1), .D2(counter09_2_d2), .D3(counter09_2_d3), .cout(counter09_2_cout));
  counter09 counter09_3 (
    .Enable(counter09_2_cout), .CLK(FASTEST_CLK), .Reset(Reset), .increment(1'b1), .D0(counter09_3_d0),
    .D1(counter09_3_d1), .D2(counter09_3_d2), .D3(counter09_3_d3), .cout(counter09_3_cout));
  counter05 counter05_1 (
    .Enable(counter09_3_cout), .CLK(FASTEST_CLK), .Reset(Reset), .increment(1'b1), .D0(counter05_1_d0),
    .D1(counter05_1_d1), .D2(counter05_1_d2), .D3(counter05_1_d3), .cout(counter05_1_cout));
  counter09 counter09_4 (
    .Enable(counter05_1_cout), .CLK(FASTEST_CLK), .Reset(Reset), .increment(1'b1), .D0(counter09_4_d0),
    .D1(counter09_4_d1), .D2(counter09_4_d2), .D3(counter09_4_d3), .cout(counter09_4_cout));
  counter05 counter05_2 (
    .Enable(counter09_4_cout), .CLK(FASTEST_CLK), .Reset(Reset), .increment(1'b1), .D0(counter05_2_d0),
    .D1(counter05_2_d1), .D2(counter05_2_d2), .D3(counter05_2_d3), .cout(counter05_2_cout));
  // NoConnect on counter05_2_cout
  seven_segment_display_decoder seven_segment_display_decoder_1 (
    .w(counter09_1_d0), .x(counter09_1_d1), .y(counter09_1_d2), .z(counter09_1_d3), .a(display0gfedcba[0]),
    .b(display0gfedcba[1]), .c(display0gfedcba[2]), .d(display0gfedcba[3]), .e(display0gfedcba[4]),
    .f(display0gfedcba[5]), .g(display0gfedcba[6]));
  seven_segment_display_decoder seven_segment_display_decoder_2 (
    .w(counter09_2_d0), .x(counter09_2_d1), .y(counter09_2_d2), .z(counter09_2_d3), .a(display1gfedcba[0]),
    .b(display1gfedcba[1]), .c(display1gfedcba[2]), .d(display1gfedcba[3]), .e(display1gfedcba[4]),
    .f(display1gfedcba[5]), .g(display1gfedcba[6]));
  seven_segment_display_decoder seven_segment_display_decoder_3 (
    .w(counter09_3_d0), .x(counter09_3_d1), .y(counter09_3_d2), .z(counter09_3_d3), .a(display2gfedcba[0]),
    .b(display2gfedcba[1]), .c(display2gfedcba[2]), .d(display2gfedcba[3]), .e(display2gfedcba[4]),
    .f(display2gfedcba[5]), .g(display2gfedcba[6]));
  seven_segment_display_decoder seven_segment_display_decoder_4 (
    .w(counter05_1_d0), .x(counter05_1_d1), .y(counter05_1_d2), .z(counter05_1_d3), .a(display3gfedcba[0]),
    .b(display3gfedcba[1]), .c(display3gfedcba[2]), .d(display3gfedcba[3]), .e(display3gfedcba[4]),
    .f(display3gfedcba[5]), .g(display3gfedcba[6]));
  seven_segment_display_decoder seven_segment_display_decoder_5 (
    .w(counter09_4_d0), .x(counter09_4_d1), .y(counter09_4_d2), .z(counter09_4_d3), .a(display4gfedcba[0]),
    .b(display4gfedcba[1]), .c(display4gfedcba[2]), .d(display4gfedcba[3]), .e(display4gfedcba[4]),
    .f(display4gfedcba[5]), .g(display4gfedcba[6]));
  seven_segment_display_decoder seven_segment_display_decoder_6 (
    .w(counter05_2_d0), .x(counter05_2_d1), .y(counter05_2_d2), .z(counter05_2_d3), .a(display5gfedcba[0]),
    .b(display5gfedcba[1]), .c(display5gfedcba[2]), .d(display5gfedcba[3]), .e(display5gfedcba[4]),
    .f(display5gfedcba[5]), .g(display5gfedcba[6]));

  // Other names for the same wires on the sheet: Clock = FASTEST_CLK
endmodule

module setting_timeee (
  input  State0,
  input  Cw,
  input  CCw,
  input  Onn,
  output increment,
  output Enable
);

  wire and_1_out, and_2_out, not_1_out, not_2_out, not_3_out;

  not not_1 (not_1_out, State0);
  not not_2 (not_2_out, Cw);
  not not_3 (not_3_out, CCw);
  or or_1 (increment, not_1_out, not_3_out, Onn);
  and and_1 (and_1_out, State0, not_2_out, CCw);
  and and_2 (and_2_out, State0, Cw, not_3_out);
  or or_2 (Enable, Onn, and_1_out, and_2_out);
endmodule

module display_selector (
  input  a_func0,
  input  a_func1,
  input  a_func2,
  input  a_func3,
  input  a_func4,
  input  a_func5,
  input  a_func6,
  input  a_func7,
  input  b_func0,
  input  b_func1,
  input  b_func2,
  input  b_func3,
  input  b_func4,
  input  b_func5,
  input  b_func6,
  input  b_func7,
  input  c_func0,
  input  c_func1,
  input  c_func2,
  input  c_func3,
  input  c_func4,
  input  c_func5,
  input  c_func6,
  input  c_func7,
  input  d_func0,
  input  d_func1,
  input  d_func2,
  input  d_func3,
  input  d_func4,
  input  d_func5,
  input  d_func6,
  input  d_func7,
  input  e_func0,
  input  e_func1,
  input  e_func2,
  input  e_func3,
  input  e_func4,
  input  e_func5,
  input  e_func6,
  input  e_func7,
  input  f_func0,
  input  f_func1,
  input  f_func2,
  input  f_func3,
  input  f_func4,
  input  f_func5,
  input  f_func6,
  input  f_func7,
  input  g_func0,
  input  g_func1,
  input  g_func2,
  input  g_func3,
  input  g_func4,
  input  g_func5,
  input  g_func6,
  input  g_func7,
  input  D2,
  input  D1,
  input  D0,
  output a_display,
  output b_display,
  output c_display,
  output d_display,
  output e_display,
  output f_display,
  output g_display
);

  Multiplexer #(.select(3)) multiplexer_1 (
    .in0(a_func0), .in1(a_func1), .in2(a_func2), .in3(a_func3), .in4(a_func4), .in5(a_func5), .in6(a_func6),
    .in7(a_func7), .out(a_display), .sel({D2, D1, D0}));
  Multiplexer #(.select(3)) multiplexer_2 (
    .in0(g_func0), .in1(g_func1), .in2(g_func2), .in3(g_func3), .in4(g_func4), .in5(g_func5), .in6(g_func6),
    .in7(g_func7), .out(g_display), .sel({D2, D1, D0}));
  Multiplexer #(.select(3)) multiplexer_3 (
    .in0(b_func0), .in1(b_func1), .in2(b_func2), .in3(b_func3), .in4(b_func4), .in5(b_func5), .in6(b_func6),
    .in7(b_func7), .out(b_display), .sel({D2, D1, D0}));
  Multiplexer #(.select(3)) multiplexer_4 (
    .in0(c_func0), .in1(c_func1), .in2(c_func2), .in3(c_func3), .in4(c_func4), .in5(c_func5), .in6(c_func6),
    .in7(c_func7), .out(c_display), .sel({D2, D1, D0}));
  Multiplexer #(.select(3)) multiplexer_5 (
    .in0(d_func0), .in1(d_func1), .in2(d_func2), .in3(d_func3), .in4(d_func4), .in5(d_func5), .in6(d_func6),
    .in7(d_func7), .out(d_display), .sel({D2, D1, D0}));
  Multiplexer #(.select(3)) multiplexer_6 (
    .in0(e_func0), .in1(e_func1), .in2(e_func2), .in3(e_func3), .in4(e_func4), .in5(e_func5), .in6(e_func6),
    .in7(e_func7), .out(e_display), .sel({D2, D1, D0}));
  Multiplexer #(.select(3)) multiplexer_7 (
    .in0(f_func0), .in1(f_func1), .in2(f_func2), .in3(f_func3), .in4(f_func4), .in5(f_func5), .in6(f_func6),
    .in7(f_func7), .out(f_display), .sel({D2, D1, D0}));
endmodule

module Timer (
  input  State3,
  input  start_stop_timer,
  input  CW,
  input  CWW,
  input  ONN,
  input  Reset,
  input  seconds_CLK,
  input  CLK_64KHz,
  input  confirm,
  output [6:0] seconds_LSD,
  output [6:0] SECONDS_MSD,
  output [6:0] MINS_LSD,
  output [6:0] MINS_MSD,
  output [6:0] HOUR_LSD,
  output [6:0] HOURS_MSD,
  output BUZZER_ON
);

  wire and_1_out, and_2_out, and_3_out, CLK, clock_1_out, clock_2_out, counter05_1_cout, counter05_2_cout,
       counter09_1_cout, counter09_2_cout, counter24h_1_cout, increment, not_1_out, not_2_out, not_3_out,
       or_1_out, or_2_out, timer_beeping_logic_and_off_1_beep, timer_beeping_logic_and_off_1_offffff,
       timer_small_logic_1_enable, toggle_button_1_outputtt, toggle_button_2_outputtt,
       toggle_button_3_outputtt, xor_1_out;
  wire [3:0] counter05_1_d0, counter05_2_d0, counter09_1_d0, counter09_2_d0;
  wire [4:0] counter24h_1_d0;

  not not_1 (not_1_out, confirm);
  and and_1 (and_1_out, State3, toggle_button_3_outputtt);
  Clock clock_1 (.out(clock_1_out));
  toggle_button toggle_button_3 (
    .Buttonn(not_1_out), .CLK(clock_1_out), .Reset(Reset), .outputtt(toggle_button_3_outputtt));
  glitch_free_mux_v2 glitch_free_mux_v2_1 (
    .SELECTT(and_1_out), .CLK1(seconds_CLK), .CLK0(CLK_64KHz), .Reset(Reset), .CLK_OUT(CLK));
  timer_small_logic timer_small_logic_1 (
    .ONNNN(ONN), .State3(State3), .start_stop(start_stop_timer), .Cw(CW), .CCw(CWW),
    .Enable(timer_small_logic_1_enable), .increment(increment));
  not not_2 (not_2_out, start_stop_timer);
  and and_2 (and_2_out, timer_beeping_logic_and_off_1_offffff, start_stop_timer);
  or or_1 (or_1_out, Reset, not_2_out);
  xor xor_1 (xor_1_out, toggle_button_1_outputtt, timer_small_logic_1_enable);
  toggle_button toggle_button_1 (.Buttonn(and_2_out), .CLK(CLK), .Reset(or_1_out), .outputtt(toggle_button_1_outputtt));
  counter09 counter09_2 (
    .Enable(counter05_1_cout), .CLK(CLK), .Reset(Reset), .increment(increment), .D0(counter09_2_d0[0]),
    .D1(counter09_2_d0[1]), .D2(counter09_2_d0[2]), .D3(counter09_2_d0[3]), .cout(counter09_2_cout));
  counter05 counter05_2 (
    .Enable(counter09_2_cout), .CLK(CLK), .Reset(Reset), .increment(increment), .D0(counter05_2_d0[0]),
    .D1(counter05_2_d0[1]), .D2(counter05_2_d0[2]), .D3(counter05_2_d0[3]), .cout(counter05_2_cout));
  counter24h counter24h_1 (
    .Enable(counter05_2_cout), .Reset(Reset), .CLK(CLK), .increment(increment), .D0(counter24h_1_d0[0]),
    .D1(counter24h_1_d0[1]), .D2(counter24h_1_d0[2]), .D3(counter24h_1_d0[3]), .D4(counter24h_1_d0[4]),
    .Cout(counter24h_1_cout));
  // NoConnect on counter24h_1_cout
  counter09 counter09_1 (
    .Enable(xor_1_out), .CLK(CLK), .Reset(Reset), .increment(increment), .D0(counter09_1_d0[0]),
    .D1(counter09_1_d0[1]), .D2(counter09_1_d0[2]), .D3(counter09_1_d0[3]), .cout(counter09_1_cout));
  counter05 counter05_1 (
    .Enable(counter09_1_cout), .CLK(CLK), .Reset(Reset), .increment(increment), .D0(counter05_1_d0[0]),
    .D1(counter05_1_d0[1]), .D2(counter05_1_d0[2]), .D3(counter05_1_d0[3]), .cout(counter05_1_cout));
  seven_segment_display_decoder seven_segment_display_decoder_3 (
    .w(counter09_2_d0[0]), .x(counter09_2_d0[1]), .y(counter09_2_d0[2]), .z(counter09_2_d0[3]),
    .a(MINS_LSD[0]), .b(MINS_LSD[1]), .c(MINS_LSD[2]), .d(MINS_LSD[3]), .e(MINS_LSD[4]), .f(MINS_LSD[5]),
    .g(MINS_LSD[6]));
  seven_segment_display_decoder seven_segment_display_decoder_4 (
    .w(counter05_2_d0[0]), .x(counter05_2_d0[1]), .y(counter05_2_d0[2]), .z(counter05_2_d0[3]),
    .a(MINS_MSD[0]), .b(MINS_MSD[1]), .c(MINS_MSD[2]), .d(MINS_MSD[3]), .e(MINS_MSD[4]), .f(MINS_MSD[5]),
    .g(MINS_MSD[6]));
  decoder24h_to_display decoder24h_to_display_1 (
    .v(counter24h_1_d0[0]), .w(counter24h_1_d0[1]), .x(counter24h_1_d0[2]), .y(counter24h_1_d0[3]),
    .z(counter24h_1_d0[4]), .a1(HOURS_MSD[0]), .b1(HOURS_MSD[1]), .c1(HOURS_MSD[2]), .d1(HOURS_MSD[3]),
    .e1(HOURS_MSD[4]), .f1(HOURS_MSD[5]), .g1(HOURS_MSD[6]), .a0(HOUR_LSD[0]), .b0(HOUR_LSD[1]),
    .c0(HOUR_LSD[2]), .d0(HOUR_LSD[3]), .e0(HOUR_LSD[4]), .f0(HOUR_LSD[5]), .g0(HOUR_LSD[6]));
  seven_segment_display_decoder seven_segment_display_decoder_1 (
    .w(counter09_1_d0[0]), .x(counter09_1_d0[1]), .y(counter09_1_d0[2]), .z(counter09_1_d0[3]),
    .a(seconds_LSD[0]), .b(seconds_LSD[1]), .c(seconds_LSD[2]), .d(seconds_LSD[3]), .e(seconds_LSD[4]),
    .f(seconds_LSD[5]), .g(seconds_LSD[6]));
  seven_segment_display_decoder seven_segment_display_decoder_2 (
    .w(counter05_1_d0[0]), .x(counter05_1_d0[1]), .y(counter05_1_d0[2]), .z(counter05_1_d0[3]),
    .a(SECONDS_MSD[0]), .b(SECONDS_MSD[1]), .c(SECONDS_MSD[2]), .d(SECONDS_MSD[3]), .e(SECONDS_MSD[4]),
    .f(SECONDS_MSD[5]), .g(SECONDS_MSD[6]));
  timer_beeping_logic_and_off timer_beeping_logic_and_off_1 (
    .seconds_LSD(counter09_1_d0), .SECONDSMSD(counter05_1_d0), .MINS_LSD(counter09_2_d0),
    .MINS_MSD(counter05_2_d0), .HOURS(counter24h_1_d0), .beep(timer_beeping_logic_and_off_1_beep),
    .offffff(timer_beeping_logic_and_off_1_offffff));
  and and_3 (and_3_out, timer_beeping_logic_and_off_1_beep, State3, ONN, start_stop_timer);
  or or_2 (or_2_out, Reset, not_3_out);
  not not_3 (not_3_out, start_stop_timer);
  toggle_button toggle_button_2 (.Buttonn(and_3_out), .CLK(CLK), .Reset(or_2_out), .outputtt(toggle_button_2_outputtt));
  Clock #(.highDuration(43), .lowDuration(43), .phaseOffset(1)) clock_2 (.out(clock_2_out));
  and and_4 (BUZZER_ON, toggle_button_2_outputtt, clock_2_out);

  // Notes on the sheet:
  //   our rotator button (CH_c pin) is logic 1 by default and when we press it it becomes logic 0
  //   i asked the prof and he said it was okay to just put a not here no need to change the card
  //   there are variations of that on the internet 
  //   it was validated by un assistant
  //   (famous glitch free Mux fpr clocks) 
  //   this is glitch free explanation in report
  //   increment-> logic 1
  //   decrement ->logic0
  //   stop the timer at 00 00 00
  //   if were at 00 00 01 stop the timer, we dont want to stop the timer of start_stop is off!
  //   fonctionne pas avec un SR latch ,S=1 R=1 ..... 
  //   Minutes MSB
  //   SECONDS MSD
  //   Minutes LSD
  //   seconds LSD
  //   Hours MSD
  //   hours LSD
  //   if we're at 00 00 01 let us know
  //   if we're at 00 00 00 start beeping
  //   TImer's beeper only works when in timer state
  //   LSD: LEAST SIGNIFICANT DIGIT
  //   MSB: MOST SIGNIFICANT DIGIT
  //   c pas grave que c une gatted clK we wont notice it 
endmodule

module timer_small_logic (
  input  ONNNN,
  input  State3,
  input  start_stop,
  input  Cw,
  input  CCw,
  output Enable,
  output increment
);

  wire and_1_out, and_2_out, and_3_out, and_4_out, not_1_out, not_2_out, not_3_out;

  not not_1 (not_1_out, ONNNN);
  not not_2 (not_2_out, start_stop);
  not not_3 (not_3_out, CCw);
  and and_1 (and_1_out, ONNNN, State3, CCw);
  and and_2 (and_2_out, ONNNN, State3, Cw);
  and and_3 (and_3_out, ONNNN, State3, start_stop);
  and and_4 (and_4_out, not_2_out, not_3_out);
  or or_1 (Enable, and_1_out, and_2_out, and_3_out);
  or or_2 (increment, not_1_out, and_4_out);
endmodule

module timer_beeping_logic_and_off (
  input  [3:0] seconds_LSD,
  input  [3:0] SECONDSMSD,
  input  [3:0] MINS_LSD,
  input  [3:0] MINS_MSD,
  input  [4:0] HOURS,
  output beep,
  output offffff
);

  wire not_1_out, not_2_out, not_3_out, not_4_out, not_5_out, not_6_out, not_7_out, not_8_out, not_9_out,
       not_10_out, not_11_out, not_12_out, not_13_out, not_14_out, not_15_out, not_16_out, not_17_out,
       not_18_out, not_19_out, not_20_out;

  not not_1 (not_1_out, SECONDSMSD[1]);
  not not_2 (not_2_out, MINS_LSD[0]);
  not not_3 (not_3_out, MINS_LSD[3]);
  not not_4 (not_4_out, MINS_MSD[1]);
  not not_5 (not_5_out, MINS_MSD[3]);
  not not_6 (not_6_out, seconds_LSD[0]);
  not not_7 (not_7_out, seconds_LSD[1]);
  not not_8 (not_8_out, seconds_LSD[2]);
  not not_9 (not_9_out, SECONDSMSD[0]);
  not not_10 (not_10_out, SECONDSMSD[2]);
  not not_11 (not_11_out, SECONDSMSD[3]);
  not not_12 (not_12_out, MINS_LSD[1]);
  not not_13 (not_13_out, MINS_LSD[2]);
  not not_14 (not_14_out, MINS_MSD[0]);
  not not_15 (not_15_out, MINS_MSD[2]);
  not not_16 (not_16_out, HOURS[0]);
  not not_17 (not_17_out, HOURS[2]);
  not not_18 (not_18_out, HOURS[3]);
  not not_19 (not_19_out, HOURS[4]);
  not not_20 (not_20_out, HOURS[1]);
  nor nor_1 (beep, seconds_LSD[0], seconds_LSD[1], seconds_LSD[2], seconds_LSD[3], SECONDSMSD[0], SECONDSMSD[1], SECONDSMSD[2], SECONDSMSD[3], MINS_LSD[0], MINS_LSD[1], MINS_LSD[2], MINS_LSD[3], MINS_MSD[0], MINS_MSD[1], MINS_MSD[2], MINS_MSD[3], HOURS[0], HOURS[1], HOURS[2], HOURS[3], HOURS[4]);
  and and_1 (offffff, not_6_out, not_7_out, not_8_out, seconds_LSD[3], not_9_out, not_1_out, not_10_out, not_11_out, not_2_out, not_12_out, not_13_out, not_3_out, not_14_out, not_4_out, not_15_out, not_5_out, not_16_out, not_20_out, not_17_out, not_18_out, not_19_out);
endmodule

module Game (
  input  Cw,
  input  CCW,
  input  Reset_game,
  input  start_stop,
  input  state_game,
  input  CLK,
  output [6:0] display0,
  output [6:0] display1,
  output [6:0] display2,
  output [6:0] display3,
  output [6:0] display4,
  output [6:0] display5
);

  wire and_1_out, and_2_out, and_3_out, and_4_out, and_5_out, and_6_out, and_7_out, and_8_out, clock_1_out,
       clock_2_out, d_ff_1_q, d_ff_1_qn, d_ff_2_q, d_ff_2_qn, d_ff_3_q, d_ff_3_qn, d_ff_4_q, d_ff_4_qn,
       d_ff_5_q, d_ff_5_qn, d_ff_6_q, d_ff_6_qn, d_ff_7_q, d_ff_7_qn, d_ff_8_q, d_ff_8_qn,
       game_filter_ish_1_signal_out, game_filter_ish_2_signal_out, not_1_out, not_2_out, not_3_out,
       not_4_out, not_5_out, not_6_out, not_7_out, not_8_out, or_1_out, or_2_out, or_3_out, or_4_out,
       random_1_out, SR_Latch_1_outttt;
  wire [6:0] game_over_1_display0, game_over_1_display1, game_over_1_display2, game_over_1_display3,
       game_over_1_display4, game_over_1_display5, gameplay_affichage_1_display0,
       gameplay_affichage_1_display1, gameplay_affichage_1_display2, gameplay_affichage_1_display3,
       gameplay_affichage_1_display4, gameplay_affichage_1_display5;

  and and_1 (and_1_out, start_stop, state_game);
  and and_2 (and_2_out, state_game, Cw);
  and and_3 (and_3_out, CCW, state_game);
  Random #(.seed(1), .width(1)) random_1 (.clr(Reset_game), .next(and_1_out), .clk(CLK), .out(random_1_out));
  or or_1 (or_1_out, and_2_out, and_3_out);
  Clock clock_1 (.out(clock_1_out));
  not not_1 (not_1_out, d_ff_6_q);
  not not_2 (not_2_out, or_1_out);
  D_Flip_Flop d_ff_1 (.D(random_1_out), .clk(CLK), .Q(d_ff_1_q), .Qn(d_ff_1_qn), .reset(Reset_game));  // open: preset
  and and_4 (and_4_out, not_1_out, or_1_out);
  and and_5 (and_5_out, d_ff_6_q, not_2_out);
  // NoConnect on d_ff_1_qn
  D_Flip_Flop d_ff_2 (.D(d_ff_1_q), .clk(CLK), .Q(d_ff_2_q), .Qn(d_ff_2_qn), .reset(Reset_game));  // open: preset
  D_Flip_Flop d_ff_3 (.D(d_ff_2_q), .clk(CLK), .Q(d_ff_3_q), .Qn(d_ff_3_qn), .reset(Reset_game));  // open: preset
  D_Flip_Flop d_ff_4 (.D(d_ff_3_q), .clk(CLK), .Q(d_ff_4_q), .Qn(d_ff_4_qn), .reset(Reset_game));  // open: preset
  D_Flip_Flop d_ff_5 (.D(d_ff_4_q), .clk(CLK), .Q(d_ff_5_q), .Qn(d_ff_5_qn), .reset(Reset_game));  // open: preset
  D_Flip_Flop d_ff_6 (
    .D(or_2_out), .clk(clock_1_out), .Q(d_ff_6_q), .Qn(d_ff_6_qn), .reset(Reset_game));  // open: preset
  or or_2 (or_2_out, and_4_out, and_5_out);
  not not_3 (not_3_out, d_ff_5_q);
  // NoConnect on d_ff_2_qn
  // NoConnect on d_ff_3_qn
  // NoConnect on d_ff_4_qn
  // NoConnect on d_ff_5_qn
  D_Flip_Flop d_ff_7 (.D(d_ff_5_q), .clk(CLK), .Q(d_ff_7_q), .Qn(d_ff_7_qn), .reset(Reset_game));  // open: preset
  D_Flip_Flop d_ff_8 (.D(not_3_out), .clk(CLK), .Q(d_ff_8_q), .Qn(d_ff_8_qn), .reset(Reset_game));  // open: preset
  // NoConnect on d_ff_7_qn
  // NoConnect on d_ff_8_qn
  game_filter_ish game_filter_ish_1 (
    .INPUT_SIGNAL(and_6_out), .CLK(CLK), .RESET(Reset_game), .SIGNAL_OUT(game_filter_ish_1_signal_out));
  and and_6 (and_6_out, d_ff_6_q, d_ff_8_q);
  and and_7 (and_7_out, d_ff_6_qn, d_ff_7_q);
  not not_4 (not_4_out, start_stop);
  or or_3 (or_3_out, game_filter_ish_1_signal_out, game_filter_ish_2_signal_out);
  or or_4 (or_4_out, not_4_out, Reset_game);
  game_filter_ish game_filter_ish_2 (
    .INPUT_SIGNAL(and_7_out), .CLK(CLK), .RESET(Reset_game), .SIGNAL_OUT(game_filter_ish_2_signal_out));
  and and_8 (and_8_out, start_stop, or_3_out);
  not not_5 (not_5_out, d_ff_3_q);
  not not_6 (not_6_out, d_ff_2_q);
  not not_7 (not_7_out, d_ff_1_q);
  not not_8 (not_8_out, d_ff_4_q);
  SR_Latch SR_Latch_1 (.Reset(or_4_out), .Set(and_8_out), .OUTTTT(SR_Latch_1_outttt));
  gameplay_affichage gameplay_affichage_1 (
    .e_4(d_ff_6_qn), .f4(d_ff_6_q), .b_5(d_ff_5_q), .c_5(not_3_out), .b_3(d_ff_3_q), .C_3(not_5_out),
    .b2(d_ff_2_q), .C2(not_6_out), .b1(d_ff_1_q), .c1(not_7_out), .b0(d_ff_4_q), .c0(not_8_out),
    .display2(gameplay_affichage_1_display2), .display1(gameplay_affichage_1_display1),
    .display3(gameplay_affichage_1_display3), .Display0(gameplay_affichage_1_display0),
    .display4(gameplay_affichage_1_display4), .display5(gameplay_affichage_1_display5));
  Clock #(.highDuration(32000), .lowDuration(32000)) clock_2 (.out(clock_2_out));
  game_over game_over_1 (
    .CLK(clock_2_out), .reset(Reset_game), .display0(game_over_1_display0), .display1(game_over_1_display1),
    .display2(game_over_1_display2), .display3(game_over_1_display3), .display4(game_over_1_display4),
    .display5(game_over_1_display5));
  Multiplexer #(.width(7)) multiplexer_1 (
    .in0(gameplay_affichage_1_display2), .in1(game_over_1_display0), .out(display0), .sel(SR_Latch_1_outttt));
  Multiplexer #(.width(7)) multiplexer_2 (
    .in0(gameplay_affichage_1_display1), .in1(game_over_1_display1), .out(display1), .sel(SR_Latch_1_outttt));
  Multiplexer #(.width(7)) multiplexer_3 (
    .in0(gameplay_affichage_1_display3), .in1(game_over_1_display2), .out(display2), .sel(SR_Latch_1_outttt));
  Multiplexer #(.width(7)) multiplexer_4 (
    .in0(gameplay_affichage_1_display0), .in1(game_over_1_display3), .out(display3), .sel(SR_Latch_1_outttt));
  Multiplexer #(.width(7)) multiplexer_5 (
    .in0(gameplay_affichage_1_display4), .in1(game_over_1_display4), .out(display4), .sel(SR_Latch_1_outttt));
  Multiplexer #(.width(7)) multiplexer_6 (
    .in0(gameplay_affichage_1_display5), .in1(game_over_1_display5), .out(display5), .sel(SR_Latch_1_outttt));

  // Other names for the same wires on the sheet: Reset = Reset_game; start_stop_game = start_stop

  // Notes on the sheet:
  //   slow_clk
  //   same logic as a bounsing filter the colision needs to last a bit for it to count
  //   f and e in the 7 segment display5
  //   current b
  //   current c
  //   previous c
  //   need to add a toggle here
  //   maybe an SR-latch
  //   slow_clk
endmodule

module game_over (
  input  CLK,
  input  reset,
  output [6:0] display0,
  output [6:0] display1,
  output [6:0] display2,
  output [6:0] display3,
  output [6:0] display4,
  output [6:0] display5
);

  wire d_ff_1_q, d_ff_1_qn, not_1_out;
  wire [6:0] game_affichage_1_display0, game_affichage_1_display1, game_affichage_1_display2,
       game_affichage_1_display3, game_affichage_1_display4, game_affichage_1_display5,
       over_affichage_1_display0, over_affichage_1_display1, over_affichage_1_display2,
       over_affichage_1_display3, over_affichage_1_display4, over_affichage_1_display5;

  not not_1 (not_1_out, d_ff_1_q);
  D_Flip_Flop d_ff_1 (.D(not_1_out), .clk(CLK), .Q(d_ff_1_q), .Qn(d_ff_1_qn), .reset(reset));  // open: preset
  // NoConnect on d_ff_1_qn
  game_affichage game_affichage_1 (
    .Display0(game_affichage_1_display0), .display1(game_affichage_1_display1),
    .display2(game_affichage_1_display2), .display3(game_affichage_1_display3),
    .display4(game_affichage_1_display4), .display5(game_affichage_1_display5));
  over_affichage over_affichage_1 (
    .Display0(over_affichage_1_display0), .display1(over_affichage_1_display1),
    .display2(over_affichage_1_display2), .display3(over_affichage_1_display3),
    .display4(over_affichage_1_display4), .display5(over_affichage_1_display5));
  Multiplexer #(.width(7)) multiplexer_1 (
    .in0(game_affichage_1_display0), .in1(over_affichage_1_display0), .out(display0), .sel(d_ff_1_q));
  Multiplexer #(.width(7)) multiplexer_2 (
    .in0(game_affichage_1_display1), .in1(over_affichage_1_display1), .out(display1), .sel(d_ff_1_q));
  Multiplexer #(.width(7)) multiplexer_3 (
    .in0(game_affichage_1_display2), .in1(over_affichage_1_display2), .out(display2), .sel(d_ff_1_q));
  Multiplexer #(.width(7)) multiplexer_4 (
    .in0(game_affichage_1_display3), .in1(over_affichage_1_display3), .out(display3), .sel(d_ff_1_q));
  Multiplexer #(.width(7)) multiplexer_5 (
    .in0(game_affichage_1_display4), .in1(over_affichage_1_display4), .out(display4), .sel(d_ff_1_q));
  Multiplexer #(.width(7)) multiplexer_6 (
    .in0(game_affichage_1_display5), .in1(over_affichage_1_display5), .out(display5), .sel(d_ff_1_q));
endmodule

module game_affichage (
  output [6:0] Display0,
  output [6:0] display1,
  output [6:0] display2,
  output [6:0] display3,
  output [6:0] display4,
  output [6:0] display5
);


  assign Display0 = {7{1'b0}};
  assign display1 = {7{1'b0}};
  assign display2 = 7'b1111001;
  assign display3 = 7'b0110111;
  assign display4 = 7'b1110111;
  assign display5 = 7'b1111101;

  // Notes on the sheet:
  //   affichage "GAME"
endmodule

module over_affichage (
  output [6:0] Display0,
  output [6:0] display1,
  output [6:0] display2,
  output [6:0] display3,
  output [6:0] display4,
  output [6:0] display5
);


  assign Display0 = {7{1'b0}};
  assign display1 = {7{1'b0}};
  assign display2 = 7'b1110111;
  assign display3 = 7'b1111001;
  assign display4 = 7'b0111110;
  assign display5 = 7'b0111111;

  // Notes on the sheet:
  //   affichage "OVER"
endmodule

module gameplay_affichage (
  input  e_4,
  input  f4,
  input  b_5,
  input  c_5,
  input  b_3,
  input  C_3,
  input  b2,
  input  C2,
  input  b1,
  input  c1,
  input  b0,
  input  c0,
  output [6:0] display2,
  output [6:0] display1,
  output [6:0] display3,
  output [6:0] Display0,
  output [6:0] display4,
  output [6:0] display5
);


  assign Display0 = {4'b0000, c0, b0, 1'b0};
  assign display1 = {4'b0000, C2, b2, 1'b0};
  assign display2 = {4'b0000, c1, b1, 1'b0};
  assign display3 = {4'b0000, C_3, b_3, 1'b0};
  assign display4 = {4'b0000, c_5, b_5, 1'b0};
  assign display5 = {1'b1, f4, {3{e_4}}, {2{f4}}};

  // Other names for the same wires on the sheet: b3 = b_3; c3 = C_3

  // Notes on the sheet:
  //   affichage du gameplay
endmodule

module SR_Latch (
  input  Reset,
  input  Set,
  output OUTTTT
);

  wire nor_2_out;

  nor nor_1 (OUTTTT, Reset, nor_2_out);
  nor nor_2 (nor_2_out, OUTTTT, Set);
endmodule

module ALARM (
  input  [20:0] current_time,
  input  ONN,
  input  State_ALARM,
  input  START_STOP_ALARM,
  input  CW,
  input  CWW,
  input  Reset,
  input  Seconds_clk,
  input  CLK64Khz,
  output [6:0] secondsLSD,
  output [6:0] Seconds_MSD,
  output [6:0] MinLSD,
  output [6:0] MINs_MSD,
  output [6:0] HOUR_LSD,
  output [6:0] HOURS_MSD,
  output Beep,
  output Output_1
);

  wire alarm_setting_1_enable, alarm_setting_1_increment, and_1_out, clock_1_out, comparator_1_eq,
       counter05_1_cout, counter05_2_cout, counter09_1_cout, counter09_2_cout, counter24h_1_cout,
       glitch_free_mux_v2_1_clk_out, not_1_out, SR_Latch_1_outttt;
  wire [3:0] mins_LSD, mins_MSD_t, seconds_LSD, seconds_MSD_t;
  wire [4:0] hours;

  glitch_free_mux_v2 glitch_free_mux_v2_1 (
    .SELECTT(ONN), .CLK1(Seconds_clk), .CLK0(CLK64Khz), .Reset(Reset), .CLK_OUT(glitch_free_mux_v2_1_clk_out));
  toggle_button toggle_button_1 (
    .Buttonn(START_STOP_ALARM), .CLK(glitch_free_mux_v2_1_clk_out), .Reset(Reset), .outputtt(Output_1));
  alarm_setting alarm_setting_1 (
    .ONNNN(ONN), .State_ALARM(State_ALARM), .START_STOP_ALARM(Output_1), .CW(CW), .CCW(CWW),
    .Enable(alarm_setting_1_enable), .increment(alarm_setting_1_increment));
  counter09 counter09_2 (
    .Enable(counter05_1_cout), .CLK(glitch_free_mux_v2_1_clk_out), .Reset(Reset),
    .increment(alarm_setting_1_increment), .D0(mins_LSD[0]), .D1(mins_LSD[1]), .D2(mins_LSD[2]),
    .D3(mins_LSD[3]), .cout(counter09_2_cout));
  counter05 counter05_2 (
    .Enable(counter09_2_cout), .CLK(glitch_free_mux_v2_1_clk_out), .Reset(Reset),
    .increment(alarm_setting_1_increment), .D0(mins_MSD_t[0]), .D1(mins_MSD_t[1]), .D2(mins_MSD_t[2]),
    .D3(mins_MSD_t[3]), .cout(counter05_2_cout));
  counter24h counter24h_1 (
    .Enable(counter05_2_cout), .Reset(Reset), .CLK(glitch_free_mux_v2_1_clk_out),
    .increment(alarm_setting_1_increment), .D0(hours[0]), .D1(hours[1]), .D2(hours[2]), .D3(hours[3]),
    .D4(hours[4]), .Cout(counter24h_1_cout));
  // NoConnect on counter24h_1_cout
  counter09 counter09_1 (
    .Enable(alarm_setting_1_enable), .CLK(glitch_free_mux_v2_1_clk_out), .Reset(Reset),
    .increment(alarm_setting_1_increment), .D0(seconds_LSD[0]), .D1(seconds_LSD[1]), .D2(seconds_LSD[2]),
    .D3(seconds_LSD[3]), .cout(counter09_1_cout));
  counter05 counter05_1 (
    .Enable(counter09_1_cout), .CLK(glitch_free_mux_v2_1_clk_out), .Reset(Reset),
    .increment(alarm_setting_1_increment), .D0(seconds_MSD_t[0]), .D1(seconds_MSD_t[1]),
    .D2(seconds_MSD_t[2]), .D3(seconds_MSD_t[3]), .cout(counter05_1_cout));
  seven_segment_display_decoder seven_segment_display_decoder_3 (
    .w(mins_LSD[0]), .x(mins_LSD[1]), .y(mins_LSD[2]), .z(mins_LSD[3]), .a(MinLSD[0]), .b(MinLSD[1]),
    .c(MinLSD[2]), .d(MinLSD[3]), .e(MinLSD[4]), .f(MinLSD[5]), .g(MinLSD[6]));
  seven_segment_display_decoder seven_segment_display_decoder_4 (
    .w(mins_MSD_t[0]), .x(mins_MSD_t[1]), .y(mins_MSD_t[2]), .z(mins_MSD_t[3]), .a(MINs_MSD[0]),
    .b(MINs_MSD[1]), .c(MINs_MSD[2]), .d(MINs_MSD[3]), .e(MINs_MSD[4]), .f(MINs_MSD[5]), .g(MINs_MSD[6]));
  decoder24h_to_display decoder24h_to_display_1 (
    .v(hours[0]), .w(hours[1]), .x(hours[2]), .y(hours[3]), .z(hours[4]), .a1(HOURS_MSD[0]),
    .b1(HOURS_MSD[1]), .c1(HOURS_MSD[2]), .d1(HOURS_MSD[3]), .e1(HOURS_MSD[4]), .f1(HOURS_MSD[5]),
    .g1(HOURS_MSD[6]), .a0(HOUR_LSD[0]), .b0(HOUR_LSD[1]), .c0(HOUR_LSD[2]), .d0(HOUR_LSD[3]),
    .e0(HOUR_LSD[4]), .f0(HOUR_LSD[5]), .g0(HOUR_LSD[6]));
  seven_segment_display_decoder seven_segment_display_decoder_1 (
    .w(seconds_LSD[0]), .x(seconds_LSD[1]), .y(seconds_LSD[2]), .z(seconds_LSD[3]), .a(secondsLSD[0]),
    .b(secondsLSD[1]), .c(secondsLSD[2]), .d(secondsLSD[3]), .e(secondsLSD[4]), .f(secondsLSD[5]),
    .g(secondsLSD[6]));
  seven_segment_display_decoder seven_segment_display_decoder_2 (
    .w(seconds_MSD_t[0]), .x(seconds_MSD_t[1]), .y(seconds_MSD_t[2]), .z(seconds_MSD_t[3]),
    .a(Seconds_MSD[0]), .b(Seconds_MSD[1]), .c(Seconds_MSD[2]), .d(Seconds_MSD[3]), .e(Seconds_MSD[4]),
    .f(Seconds_MSD[5]), .g(Seconds_MSD[6]));
  Comparator #(.width(21)) comparator_1 (
    .a({hours, mins_MSD_t, mins_LSD, seconds_MSD_t, seconds_LSD}), .b(current_time), .eq(comparator_1_eq));  // open: gt, lt
  not not_1 (not_1_out, Output_1);
  and and_1 (and_1_out, comparator_1_eq, Output_1, ONN);
  SR_Latch SR_Latch_1 (.Reset(not_1_out), .Set(and_1_out), .OUTTTT(SR_Latch_1_outttt));
  Clock #(.highDuration(43), .lowDuration(43), .phaseOffset(1)) clock_1 (.out(clock_1_out));
  and and_2 (Beep, SR_Latch_1_outttt, clock_1_out);

  // Other names for the same wires on the sheet: alarm_on = Output_1; watch_on = ONN

  // Notes on the sheet:
  //   increment-> logic 1
  //   decrement ->logic0
  //   5 bits
  //   4 bits
  //   4 bits
  //   4 bits
  //   4 bits
  //   Minutes LSd
  //   Minutes MSD
  //   SECONDS MSd
  //   seconds LSdigit
  //   Hours MSB
  //   hours LSB
  //   dont care about the gated clock
endmodule

module alarm_setting (
  input  ONNNN,
  input  State_ALARM,
  input  START_STOP_ALARM,
  input  CW,
  input  CCW,
  output Enable,
  output increment
);

  wire and_1_out, and_2_out, not_1_out, not_2_out;

  not not_1 (not_1_out, START_STOP_ALARM);
  not not_2 (not_2_out, CW);
  not not_3 (increment, CCW);
  and and_1 (and_1_out, ONNNN, State_ALARM, not_1_out, not_2_out, CCW);
  and and_2 (and_2_out, ONNNN, State_ALARM, not_1_out, CW, increment);
  or or_1 (Enable, and_1_out, and_2_out);
endmodule

module game10sec (
  input  START1_STOP0,
  input  Reset,
  input  FASTEST_CLK,
  input  State7,
  output [6:0] display5,
  output [6:0] display4,
  output [6:0] display3,
  output [6:0] display2,
  output [6:0] display1,
  output [6:0] display0
);

  wire and_1_out, counter05_1_cout, counter05_2_cout, counter09_1_cout, counter09_2_cout, counter09_3_cout,
       counter09_4_cout;
  wire [3:0] counter05_2_d0;
  wire [19:0] counter09_1_d0;

  and and_1 (and_1_out, START1_STOP0, State7);
  counter09 counter09_1 (
    .Enable(and_1_out), .CLK(FASTEST_CLK), .Reset(Reset), .increment(1'b1), .D0(counter09_1_d0[0]),
    .D1(counter09_1_d0[1]), .D2(counter09_1_d0[2]), .D3(counter09_1_d0[3]), .cout(counter09_1_cout));
  counter09 counter09_2 (
    .Enable(counter09_1_cout), .CLK(FASTEST_CLK), .Reset(Reset), .increment(1'b1), .D0(counter09_1_d0[4]),
    .D1(counter09_1_d0[5]), .D2(counter09_1_d0[6]), .D3(counter09_1_d0[7]), .cout(counter09_2_cout));
  counter09 counter09_3 (
    .Enable(counter09_2_cout), .CLK(FASTEST_CLK), .Reset(Reset), .increment(1'b1), .D0(counter09_1_d0[8]),
    .D1(counter09_1_d0[9]), .D2(counter09_1_d0[10]), .D3(counter09_1_d0[11]), .cout(counter09_3_cout));
  counter05 counter05_1 (
    .Enable(counter09_3_cout), .CLK(FASTEST_CLK), .Reset(Reset), .increment(1'b1), .D0(counter09_1_d0[12]),
    .D1(counter09_1_d0[13]), .D2(counter09_1_d0[14]), .D3(counter09_1_d0[15]), .cout(counter05_1_cout));
  counter09 counter09_4 (
    .Enable(counter05_1_cout), .CLK(FASTEST_CLK), .Reset(Reset), .increment(1'b1), .D0(counter09_1_d0[16]),
    .D1(counter09_1_d0[17]), .D2(counter09_1_d0[18]), .D3(counter09_1_d0[19]), .cout(counter09_4_cout));
  counter05 counter05_2 (
    .Enable(counter09_4_cout), .CLK(FASTEST_CLK), .Reset(Reset), .increment(1'b1), .D0(counter05_2_d0[0]),
    .D1(counter05_2_d0[1]), .D2(counter05_2_d0[2]), .D3(counter05_2_d0[3]), .cout(counter05_2_cout));
  // NoConnect on counter05_2_cout
  game_logic10sec game_logic10sec_1 (
    .start_stop(START1_STOP0), .current_time({counter05_2_d0, counter09_1_d0}), .Reset(Reset),
    .display5(display5), .display4(display4), .display3(display3), .display2(display2), .display1(display1),
    .display0(display0));

  // Other names for the same wires on the sheet: Clock = FASTEST_CLK

  // Notes on the sheet:
  //   100th of a sec
  //   10th of a sec
  //   second LSD
endmodule

module game_filter_ish (
  input  INPUT_SIGNAL,
  input  CLK,
  input  RESET,
  output SIGNAL_OUT
);

  wire d_ff_1_q, d_ff_1_qn, d_ff_2_q, d_ff_2_qn, d_ff_3_q, d_ff_3_qn;

  D_Flip_Flop d_ff_1 (.D(INPUT_SIGNAL), .clk(CLK), .Q(d_ff_1_q), .Qn(d_ff_1_qn), .reset(RESET));  // open: preset
  // NoConnect on d_ff_1_qn
  D_Flip_Flop d_ff_2 (.D(d_ff_1_q), .clk(CLK), .Q(d_ff_2_q), .Qn(d_ff_2_qn), .reset(RESET));  // open: preset
  D_Flip_Flop d_ff_3 (.D(d_ff_2_q), .clk(CLK), .Q(d_ff_3_q), .Qn(d_ff_3_qn), .reset(RESET));  // open: preset
  // NoConnect on d_ff_3_qn
  // NoConnect on d_ff_2_qn
  and and_1 (SIGNAL_OUT, d_ff_1_q, d_ff_2_q, d_ff_3_q);
endmodule

module game_logic10sec (
  input  start_stop,
  input  [23:0] current_time,
  input  Reset,
  output [6:0] display5,
  output [6:0] display4,
  output [6:0] display3,
  output [6:0] display2,
  output [6:0] display1,
  output [6:0] display0
);

  wire affiche_nothing, and_1_out, clock_1_out, comparator_1_eq, comparator_1_gt, comparator_1_lt, d_ff_1_q,
       d_ff_1_qn, not_1_out, not_2_out, not_3_out, won_lost;
  wire [41:0] affichage_nothing_1_displays5_1, loser_affichage_1_displays5_1, multiplexer_1_out,
       multiplexer_2_out, SCORE_affichage_1_displays5_1, time_10_sec_game_affichage_1_displays5_1;

  and and_1 (and_1_out, ~current_time[0], ~current_time[1], ~current_time[2], ~current_time[3], ~current_time[4], ~current_time[5], ~current_time[6], ~current_time[7], ~current_time[8], ~current_time[9], ~current_time[10], ~current_time[11], ~current_time[12], ~current_time[13], ~current_time[14], ~current_time[15], ~current_time[16], ~current_time[17], ~current_time[18], ~current_time[19], ~current_time[20], ~current_time[21], ~current_time[22], ~current_time[23]);  // AND_Gate
  not not_1 (not_1_out, and_1_out);
  not not_2 (not_2_out, start_stop);
  or or_1 (affiche_nothing, start_stop, and_1_out);
  loser_affichage loser_affichage_1 (.displays5_1(loser_affichage_1_displays5_1));
  SCORE_affichage SCORE_affichage_1 (.displays5_1(SCORE_affichage_1_displays5_1));
  Clock #(.highDuration(32000), .lowDuration(32000)) clock_1 (.out(clock_1_out));
  // NoConnect on comparator_1_gt
  Comparator #(.width(24)) comparator_1 (
    .a(24'h1000), .b(current_time), .gt(comparator_1_gt), .eq(comparator_1_eq), .lt(comparator_1_lt));
  // NoConnect on comparator_1_lt
  Multiplexer #(.width(42)) multiplexer_1 (
    .in0(loser_affichage_1_displays5_1), .in1(SCORE_affichage_1_displays5_1), .out(multiplexer_1_out),
    .sel(won_lost));
  D_Flip_Flop d_ff_1 (.D(not_3_out), .clk(clock_1_out), .Q(d_ff_1_q), .Qn(d_ff_1_qn), .reset(Reset));  // open: preset
  not not_3 (not_3_out, d_ff_1_q);
  // NoConnect on d_ff_1_qn
  and and_2 (won_lost, not_1_out, not_2_out, comparator_1_eq);
  time_10_sec_game_affichage time_10_sec_game_affichage_1 (
    .current_time(current_time), .displays5_1(time_10_sec_game_affichage_1_displays5_1));
  Multiplexer #(.width(42)) multiplexer_2 (
    .in0(multiplexer_1_out), .in1(time_10_sec_game_affichage_1_displays5_1), .out(multiplexer_2_out),
    .sel(d_ff_1_q));
  Multiplexer #(.width(42)) multiplexer_3 (
    .in0(multiplexer_2_out), .in1(affichage_nothing_1_displays5_1),
    .out({display0, display1, display2, display3, display4, display5}), .sel(affiche_nothing));
  affichage_nothing affichage_nothing_1 (.displays5_1(affichage_nothing_1_displays5_1));

  // Notes on the sheet:
  //   10 seconds: 0000 0000 0001 0000 0000 0000 in binary is 0x1000
  //   affiche nothing
  //   if current time != 00 00 00 and start stop=0
  //   affichage clk
  //   or if its on
  //   if current time == 00 00 00 ->affichage = nothing (all 0)
  //   0 you lost ;1 you won
  //   displays
endmodule
module affichage_nothing (
  output [41:0] displays5_1
);


  assign displays5_1 = {42{1'b0}};
endmodule

module loser_affichage (
  output [41:0] displays5_1
);


  assign displays5_1 = 42'h77f3b5fb8;

  // Notes on the sheet:
  //   L
  //   O
  //   S
  //   E
  //   R
  //   display5
  //   display4
  //   display3
  //   display2
  //   display1
  //   display0
endmodule

module SCORE_affichage (
  output [41:0] displays5_1
);


  assign displays5_1 = 42'h79eefdced;

  // Notes on the sheet:
  //   S
  //   R
  //   E
  //   display5
  //   C
  //   O
  //   display4
  //   display3
  //   display2
  //   display1
  //   display0
endmodule

module time_10_sec_game_affichage (
  input  [23:0] current_time,
  output [41:0] displays5_1
);

  seven_segment_display_decoder seven_segment_display_decoder_1 (
    .w(current_time[0]), .x(current_time[1]), .y(current_time[2]), .z(current_time[3]), .a(displays5_1[35]),
    .b(displays5_1[36]), .c(displays5_1[37]), .d(displays5_1[38]), .e(displays5_1[39]), .f(displays5_1[40]),
    .g(displays5_1[41]));
  seven_segment_display_decoder seven_segment_display_decoder_2 (
    .w(current_time[4]), .x(current_time[5]), .y(current_time[6]), .z(current_time[7]), .a(displays5_1[28]),
    .b(displays5_1[29]), .c(displays5_1[30]), .d(displays5_1[31]), .e(displays5_1[32]), .f(displays5_1[33]),
    .g(displays5_1[34]));
  seven_segment_display_decoder seven_segment_display_decoder_3 (
    .w(current_time[8]), .x(current_time[9]), .y(current_time[10]), .z(current_time[11]),
    .a(displays5_1[21]), .b(displays5_1[22]), .c(displays5_1[23]), .d(displays5_1[24]), .e(displays5_1[25]),
    .f(displays5_1[26]), .g(displays5_1[27]));
  seven_segment_display_decoder seven_segment_display_decoder_4 (
    .w(current_time[12]), .x(current_time[13]), .y(current_time[14]), .z(current_time[15]),
    .a(displays5_1[14]), .b(displays5_1[15]), .c(displays5_1[16]), .d(displays5_1[17]), .e(displays5_1[18]),
    .f(displays5_1[19]), .g(displays5_1[20]));
  seven_segment_display_decoder seven_segment_display_decoder_5 (
    .w(current_time[16]), .x(current_time[17]), .y(current_time[18]), .z(current_time[19]),
    .a(displays5_1[7]), .b(displays5_1[8]), .c(displays5_1[9]), .d(displays5_1[10]), .e(displays5_1[11]),
    .f(displays5_1[12]), .g(displays5_1[13]));
  seven_segment_display_decoder seven_segment_display_decoder_6 (
    .w(current_time[20]), .x(current_time[21]), .y(current_time[22]), .z(current_time[23]),
    .a(displays5_1[0]), .b(displays5_1[1]), .c(displays5_1[2]), .d(displays5_1[3]), .e(displays5_1[4]),
    .f(displays5_1[5]), .g(displays5_1[6]));

  // Notes on the sheet:
  //   display3
  //   display4
  //   display1
  //   display2
  //   display0
  //   display5
  //   display5
  //   display4
  //   display3
  //   display2
  //   display1
  //   display0
endmodule

module MP3 (
  input  state_MP3,
  input  ON_OFF_MUSIC,
  input  SONG_SELECTOR,
  output pin2_buzzer,
  output [6:0] display5,
  output [6:0] display4,
  output [6:0] display3,
  output [6:0] display2,
  output [6:0] display1,
  output [6:0] display0
);

  wire and_1_out, and_2_out, and_3_out, and_4_out, and_5_out, and_6_out, and_7_out, CLK_out, not_1_out,
       or_1_out, or_2_out, song1_1_a4, song1_1_b4, song1_1_do4, song1_1_do5, song1_1_dsharp5, song1_1_e4,
       song1_1_e5, song1_1_gsharp, song1_1_pin2_buzzer, song1_1_re5, song2_1_b4, song2_1_db5, song2_1_e5,
       song2_1_fsharp5, song2_1_g4, song2_1_pin2_buzzer, song2_1_re5;

  Clock #(.highDuration(16000), .lowDuration(16000)) CLK (.out(CLK_out));
  and and_1 (and_1_out, state_MP3, ON_OFF_MUSIC);
  song1 song1_1 (
    .ON_OFF(and_1_out), .CLK(CLK_out), .pin2_buzzer(song1_1_pin2_buzzer), .E5(song1_1_e5),
    .Dsharp5(song1_1_dsharp5), .B4(song1_1_b4), .re5(song1_1_re5), .do5(song1_1_do5), .A4(song1_1_a4),
    .do4(song1_1_do4), .E4(song1_1_e4), .Gsharp(song1_1_gsharp));
  song2 song2_1 (
    .on_off(and_1_out), .CLk(CLK_out), .pin2_buzzer(song2_1_pin2_buzzer), .Fsharp5(song2_1_fsharp5),
    .B4(song2_1_b4), .Db5(song2_1_db5), .re5(song2_1_re5), .E5(song2_1_e5), .G4(song2_1_g4));
  Multiplexer multiplexer_1 (
    .in0(song1_1_pin2_buzzer), .in1(song2_1_pin2_buzzer), .out(pin2_buzzer), .sel(SONG_SELECTOR));
  or or_1 (or_1_out, song1_1_e5, song1_1_e4);
  and and_2 (and_2_out, not_1_out, or_1_out);
  and and_3 (and_3_out, SONG_SELECTOR, song2_1_e5);
  not not_1 (not_1_out, SONG_SELECTOR);
  and and_4 (and_4_out, song1_1_re5, not_1_out);
  and and_5 (and_5_out, SONG_SELECTOR, song2_1_re5);
  and and_6 (and_6_out, song1_1_b4, not_1_out);
  and and_7 (and_7_out, song2_1_b4, SONG_SELECTOR);
  or or_2 (or_2_out, song1_1_do5, song1_1_do4);
  and and_8 (display0[1], SONG_SELECTOR, song2_1_db5);
  and and_9 (display0[4], not_1_out, or_2_out);
  and and_10 (display1[1], song1_1_dsharp5, not_1_out);
  or or_3 (display1[4], and_4_out, and_5_out);
  or or_4 (display2[4], and_2_out, and_3_out);
  and and_11 (display3[2], song2_1_g4, SONG_SELECTOR);
  and and_12 (display3[5], song2_1_fsharp5, SONG_SELECTOR);
  and and_13 (display4[2], song1_1_a4, not_1_out);
  and and_14 (display4[5], song1_1_gsharp, not_1_out);
  or or_5 (display5[2], and_6_out, and_7_out);

  assign {display0[6:5], display0[3:2], display0[0]} = {5{1'b0}};
  assign {display1[6:5], display1[3:2], display1[0]} = {5{1'b0}};
  assign {display2[6:5], display2[3:0]} = {6{1'b0}};
  assign {display3[6], display3[4:3], display3[1:0]} = {5{1'b0}};
  assign {display4[6], display4[4:3], display4[1:0]} = {5{1'b0}};
  assign {display5[6:3], display5[1:0]} = {6{1'b0}};

  // Notes on the sheet:
  //   0->song1
  //   1->song 2
  //   a display0
  //   b display0
  //   c display0
  //   d display0
  //   e display0
  //   f display0
  //   g display0
  //   a display1
  //   b display1
  //   c display1
  //   d display1
  //   e display1
  //   f display1
  //   g display1
  //   a display2
  //   b display2
  //   c display2
  //   d display2
  //   e display2
  //   f display2
  //   g display2
  //   a display3
  //   b display3
  //   c display3
  //   d display3
  //   e display3
  //   f display3
  //   g display3
  //   a display4
  //   b display4
  //   c display4
  //   d display4
  //   e display4
  //   f display4
  //   g display4
  //   a display5
  //   b display5
  //   c display5
  //   d display5
  //   e display5
  //   f display5
  //   g display5
endmodule

module song1_fsm_transition_logic (
  input  C5,
  input  C4,
  input  C3,
  input  C2,
  input  C1,
  input  C0,
  output D5,
  output D4,
  output D3,
  output D2,
  output D1,
  output D0
);

  wire and_1_out, and_2_out, and_3_out, and_4_out, and_5_out, and_6_out, and_7_out, and_8_out, and_9_out,
       and_10_out, and_11_out, and_12_out, and_13_out, and_14_out, and_15_out, and_16_out, and_17_out,
       and_18_out, not_1_out, not_2_out, not_3_out, not_4_out, not_5_out;

  not not_1 (not_1_out, C5);
  not not_2 (not_2_out, C4);
  not not_3 (not_3_out, C3);
  not not_4 (not_4_out, C2);
  not not_5 (not_5_out, C1);
  not not_6 (D0, C0);
  and and_1 (and_1_out, C4, C3, C2, C1, C0);
  and and_2 (and_2_out, C5, not_4_out);
  and and_3 (and_3_out, C5, not_5_out);
  and and_4 (and_4_out, C5, D0);
  and and_5 (and_5_out, not_2_out, C3, C2, C1, C0);
  and and_6 (and_6_out, C4, not_3_out);
  and and_7 (and_7_out, C4, not_4_out);
  and and_8 (and_8_out, C4, not_5_out);
  and and_9 (and_9_out, C4, D0);
  and and_10 (and_10_out, not_1_out, not_3_out, C2, C1, C0);
  and and_11 (and_11_out, C3, not_4_out);
  and and_12 (and_12_out, C3, not_5_out);
  and and_13 (and_13_out, C3, D0);
  and and_14 (and_14_out, not_4_out, C1, C0);
  and and_15 (and_15_out, C2, not_5_out);
  and and_16 (and_16_out, C2, D0);
  and and_17 (and_17_out, not_5_out, C0);
  and and_18 (and_18_out, C1, D0);
  or or_1 (D5, and_1_out, and_2_out, and_3_out, and_4_out);
  or or_2 (D4, and_5_out, and_6_out, and_7_out, and_8_out, and_9_out);
  or or_3 (D3, and_10_out, and_11_out, and_12_out, and_13_out);
  or or_4 (D2, and_14_out, and_15_out, and_16_out);
  or or_5 (D1, and_17_out, and_18_out);
endmodule

module song1_decoder (
  input  D5,
  input  D4,
  input  D3,
  input  D2,
  input  D1,
  input  D0,
  output E5,
  output Dsharp5,
  output B4,
  output re5,
  output do5,
  output A4,
  output do4,
  output E4,
  output Gsharp4
);

  wire and_1_out, and_2_out, and_3_out, and_4_out, and_5_out, and_6_out, and_7_out, and_8_out, and_9_out,
       and_10_out, and_11_out, and_12_out, and_13_out, and_14_out, and_15_out, and_16_out, and_17_out,
       and_18_out, and_19_out, and_20_out, and_21_out, and_22_out, and_23_out, and_24_out, and_25_out,
       and_26_out, and_27_out, not_1_out, not_2_out, not_3_out, not_4_out, not_5_out, not_6_out;

  not not_1 (not_1_out, D5);
  not not_2 (not_2_out, D4);
  not not_3 (not_3_out, D3);
  not not_4 (not_4_out, D2);
  not not_5 (not_5_out, D1);
  not not_6 (not_6_out, D0);
  and and_1 (and_1_out, D4, not_3_out, D2, not_6_out);
  and and_2 (and_2_out, D4, D3, not_4_out, not_5_out, not_6_out);
  and and_3 (and_3_out, not_1_out, not_2_out, not_3_out, not_4_out, not_6_out);
  and and_4 (and_4_out, not_1_out, not_2_out, not_3_out, not_5_out, not_6_out);
  and and_5 (and_5_out, not_1_out, not_2_out, not_3_out, not_4_out, D0);
  and and_6 (and_6_out, D4, not_3_out, D2, D0);
  and and_7 (and_7_out, D4, not_4_out, not_5_out, D0);
  and and_8 (and_8_out, D5, not_5_out, D0);
  and and_9 (and_9_out, D5, not_4_out, D1, not_6_out);
  and and_10 (and_10_out, not_2_out, D2, not_5_out, D0);
  and and_11 (and_11_out, not_2_out, D3, D2, D1, not_6_out);
  and and_12 (and_12_out, not_1_out, not_2_out, not_3_out, D2, D1, not_6_out);
  and and_13 (and_13_out, D4, D3, not_4_out, D1, not_6_out);
  and and_14 (and_14_out, D4, not_3_out, not_4_out, D1);
  and and_15 (and_15_out, D5, D2, not_5_out, not_6_out);
  and and_16 (and_16_out, not_1_out, not_2_out, not_3_out, D2, D1, D0);
  and and_17 (and_17_out, D4, not_4_out, D1, D0);
  and and_18 (and_18_out, D5, not_4_out, not_5_out, not_6_out);
  and and_19 (and_19_out, D5, D2, D1);
  and and_20 (and_20_out, not_2_out, D3, not_4_out, not_5_out);
  and and_21 (and_21_out, D4, D3, D2, not_5_out);
  and and_22 (and_22_out, not_2_out, D3, not_5_out, not_6_out);
  and and_23 (and_23_out, not_2_out, D3, not_4_out, D1, not_6_out);
  and and_24 (and_24_out, D4, D3, D2, D1, not_6_out);
  and and_25 (and_25_out, D5, not_4_out, D1, D0);
  and and_26 (and_26_out, not_2_out, D3, D1, D0);
  and and_27 (and_27_out, D3, D2, D1, D0);
  and and_28 (Gsharp4, D4, not_3_out, not_4_out, not_5_out, not_6_out);
  or or_1 (E5, and_1_out, and_2_out, and_3_out, and_4_out);
  or or_2 (Dsharp5, and_5_out, and_6_out);
  or or_3 (B4, and_7_out, and_8_out, and_9_out, and_10_out, and_11_out);
  or or_4 (re5, and_12_out, and_13_out);
  or or_5 (do5, and_14_out, and_15_out, and_16_out, and_17_out);
  or or_6 (A4, and_18_out, and_19_out, and_20_out, and_21_out, and_22_out);
  or or_7 (do4, and_23_out, and_24_out);
  or or_8 (E4, and_25_out, and_26_out, and_27_out);
endmodule

module song1_64k_frequence (
  input  E5,
  input  Dsharp5,
  input  B4,
  input  re5,
  input  do5,
  input  A4,
  input  do4,
  input  E4,
  input  Gsharp4,
  output song1_note
);

  wire A4_clock_out, and_1_out, and_2_out, and_3_out, and_4_out, and_5_out, and_6_out, and_7_out, and_8_out,
       and_9_out, B4_clock_out, do4_clock_out, do5_clock_out, Dsharp5_clock_out, E4_clock_out, E5_clock_out,
       Gsharp4_clock_out, re5_clock_out;

  Clock #(.highDuration(49), .lowDuration(49)) E5_clock (.out(E5_clock_out));
  Clock #(.highDuration(51), .lowDuration(51)) Dsharp5_clock (.out(Dsharp5_clock_out));
  Clock #(.highDuration(65), .lowDuration(65)) B4_clock (.out(B4_clock_out));
  Clock #(.highDuration(54), .lowDuration(54)) re5_clock (.out(re5_clock_out));
  Clock #(.highDuration(61), .lowDuration(61)) do5_clock (.out(do5_clock_out));
  Clock #(.highDuration(73), .lowDuration(73)) A4_clock (.out(A4_clock_out));
  Clock #(.highDuration(122), .lowDuration(122)) do4_clock (.out(do4_clock_out));
  Clock #(.highDuration(97), .lowDuration(97)) E4_clock (.out(E4_clock_out));
  Clock #(.highDuration(77), .lowDuration(77)) Gsharp4_clock (.out(Gsharp4_clock_out));
  and and_1 (and_1_out, E5, E5_clock_out);
  and and_2 (and_2_out, Dsharp5, Dsharp5_clock_out);
  and and_3 (and_3_out, B4, B4_clock_out);
  and and_4 (and_4_out, re5, re5_clock_out);
  and and_5 (and_5_out, do5, do5_clock_out);
  and and_6 (and_6_out, A4, A4_clock_out);
  and and_7 (and_7_out, do4, do4_clock_out);
  and and_8 (and_8_out, E4, E4_clock_out);
  and and_9 (and_9_out, Gsharp4, Gsharp4_clock_out);
  or or_1 (song1_note, and_1_out, and_2_out, and_3_out, and_4_out, and_5_out, and_6_out, and_7_out, and_8_out, and_9_out);

  // Notes on the sheet:
  //   gated clocks aren't a problem here, we won't hear it if there's a glitch
endmodule

module song1 (
  input  ON_OFF,
  input  CLK,
  output pin2_buzzer,
  output E5,
  output Dsharp5,
  output B4,
  output re5,
  output do5,
  output A4,
  output do4,
  output E4,
  output Gsharp
);

  wire d_ff_1_q, d_ff_1_qn, d_ff_2_q, d_ff_2_qn, d_ff_3_q, d_ff_3_qn, d_ff_4_q, d_ff_4_qn, d_ff_5_q,
       d_ff_5_qn, d_ff_6_q, d_ff_6_qn, not_1_out, song1_64k_frequence_1_song1_note,
       song1_fsm_transition_logic_1_d0, song1_fsm_transition_logic_1_d1, song1_fsm_transition_logic_1_d2,
       song1_fsm_transition_logic_1_d3, song1_fsm_transition_logic_1_d4, song1_fsm_transition_logic_1_d5;

  not not_1 (not_1_out, ON_OFF);
  song1_fsm_transition_logic song1_fsm_transition_logic_1 (
    .C5(d_ff_1_q), .C4(d_ff_2_q), .C3(d_ff_3_q), .C2(d_ff_4_q), .C1(d_ff_5_q), .C0(d_ff_6_q),
    .D5(song1_fsm_transition_logic_1_d5), .D4(song1_fsm_transition_logic_1_d4),
    .D3(song1_fsm_transition_logic_1_d3), .D2(song1_fsm_transition_logic_1_d2),
    .D1(song1_fsm_transition_logic_1_d1), .D0(song1_fsm_transition_logic_1_d0));
  D_Flip_Flop d_ff_1 (
    .D(song1_fsm_transition_logic_1_d5), .clk(CLK), .Q(d_ff_1_q), .Qn(d_ff_1_qn), .reset(not_1_out));  // open: preset
  // NoConnect on d_ff_1_qn
  D_Flip_Flop d_ff_2 (
    .D(song1_fsm_transition_logic_1_d4), .clk(CLK), .Q(d_ff_2_q), .Qn(d_ff_2_qn), .reset(not_1_out));  // open: preset
  // NoConnect on d_ff_2_qn
  D_Flip_Flop d_ff_3 (
    .D(song1_fsm_transition_logic_1_d3), .clk(CLK), .Q(d_ff_3_q), .Qn(d_ff_3_qn), .reset(not_1_out));  // open: preset
  // NoConnect on d_ff_3_qn
  D_Flip_Flop d_ff_4 (
    .D(song1_fsm_transition_logic_1_d2), .clk(CLK), .Q(d_ff_4_q), .Qn(d_ff_4_qn), .reset(not_1_out));  // open: preset
  // NoConnect on d_ff_4_qn
  D_Flip_Flop d_ff_5 (
    .D(song1_fsm_transition_logic_1_d1), .clk(CLK), .Q(d_ff_5_q), .Qn(d_ff_5_qn), .reset(not_1_out));  // open: preset
  // NoConnect on d_ff_5_qn
  D_Flip_Flop d_ff_6 (
    .D(song1_fsm_transition_logic_1_d0), .clk(CLK), .Q(d_ff_6_q), .Qn(d_ff_6_qn), .reset(not_1_out));  // open: preset
  // NoConnect on d_ff_6_qn
  song1_decoder song1_decoder_1 (
    .D5(d_ff_1_q), .D4(d_ff_2_q), .D3(d_ff_3_q), .D2(d_ff_4_q), .D1(d_ff_5_q), .D0(d_ff_6_q), .E5(E5),
    .Dsharp5(Dsharp5), .B4(B4), .re5(re5), .do5(do5), .A4(A4), .do4(do4), .E4(E4), .Gsharp4(Gsharp));
  song1_64k_frequence song1_64k_frequence_1 (
    .E5(E5), .Dsharp5(Dsharp5), .B4(B4), .re5(re5), .do5(do5), .A4(A4), .do4(do4), .E4(E4), .Gsharp4(Gsharp),
    .song1_note(song1_64k_frequence_1_song1_note));
  and and_1 (pin2_buzzer, song1_64k_frequence_1_song1_note, ON_OFF);
endmodule

module song2_fsm_transition_logic (
  input  C5,
  input  C4,
  input  C3,
  input  C2,
  input  C1,
  input  C0,
  output D5,
  output D4,
  output D3,
  output D2,
  output D1,
  output D0
);

  wire and_1_out, and_2_out, and_3_out, and_4_out, and_5_out, and_6_out, and_7_out, and_8_out, and_9_out,
       and_10_out, and_11_out, and_12_out, and_13_out, and_14_out, and_15_out, and_16_out, and_17_out,
       and_18_out, and_19_out, and_20_out, and_21_out, and_22_out, and_23_out, and_24_out, and_25_out,
       not_1_out, not_2_out, not_3_out, not_4_out, not_5_out, not_6_out;

  not not_1 (not_1_out, C5);
  not not_2 (not_2_out, C4);
  not not_3 (not_3_out, C3);
  not not_4 (not_4_out, C2);
  not not_5 (not_5_out, C1);
  not not_6 (not_6_out, C0);
  and and_1 (and_1_out, C5, not_2_out);
  and and_2 (and_2_out, C5, not_4_out);
  and and_3 (and_3_out, C5, not_5_out);
  and and_4 (and_4_out, C4, C3, C2, C1, C0);
  and and_5 (and_5_out, not_2_out, C3, C2, C1, C0);
  and and_6 (and_6_out, C4, not_4_out);
  and and_7 (and_7_out, C4, not_5_out);
  and and_8 (and_8_out, not_1_out, C4, not_3_out);
  and and_9 (and_9_out, not_1_out, C4, not_6_out);
  and and_10 (and_10_out, not_3_out, C2, C1, C0);
  and and_11 (and_11_out, C3, not_4_out);
  and and_12 (and_12_out, C3, not_5_out);
  and and_13 (and_13_out, C3, not_6_out);
  and and_14 (and_14_out, not_4_out, C1, C0);
  and and_15 (and_15_out, C2, not_5_out);
  and and_16 (and_16_out, not_1_out, C2, not_6_out);
  and and_17 (and_17_out, not_2_out, C2, not_6_out);
  and and_18 (and_18_out, not_5_out, C0);
  and and_19 (and_19_out, not_1_out, C1, not_6_out);
  and and_20 (and_20_out, not_2_out, C1, not_6_out);
  and and_21 (and_21_out, not_4_out, C1, not_6_out);
  and and_22 (and_22_out, not_1_out, not_6_out);
  and and_23 (and_23_out, not_2_out, not_6_out);
  and and_24 (and_24_out, not_4_out, not_6_out);
  and and_25 (and_25_out, not_5_out, not_6_out);
  or or_1 (D5, and_1_out, and_2_out, and_3_out, and_4_out);
  or or_2 (D4, and_5_out, and_6_out, and_7_out, and_8_out, and_9_out);
  or or_3 (D3, and_10_out, and_11_out, and_12_out, and_13_out);
  or or_4 (D2, and_14_out, and_15_out, and_16_out, and_17_out);
  or or_5 (D1, and_18_out, and_19_out, and_20_out, and_21_out);
  or or_6 (D0, and_22_out, and_23_out, and_24_out, and_25_out);
endmodule

module song2_decoder (
  input  D5,
  input  D4,
  input  D3,
  input  D2,
  input  D1,
  input  D0,
  output Fsharp5,
  output B4,
  output Db5,
  output re5,
  output E5,
  output G4
);

  wire and_1_out, and_2_out, and_3_out, and_4_out, and_5_out, and_6_out, and_7_out, and_8_out, and_9_out,
       and_10_out, and_11_out, and_12_out, and_13_out, and_14_out, and_15_out, and_16_out, and_17_out,
       and_18_out, and_19_out, and_20_out, and_21_out, and_22_out, and_23_out, and_24_out, and_25_out,
       and_26_out, and_27_out, and_28_out, and_29_out, and_30_out, and_31_out, and_32_out, not_1_out,
       not_2_out, not_3_out, not_4_out, not_5_out, not_6_out;

  not not_1 (not_1_out, D5);
  not not_2 (not_2_out, D4);
  not not_3 (not_3_out, D3);
  not not_4 (not_4_out, D2);
  not not_5 (not_5_out, D1);
  not not_6 (not_6_out, D0);
  and and_1 (and_1_out, not_1_out, not_2_out, not_3_out, not_4_out);
  and and_2 (and_2_out, not_1_out, not_2_out, D3, not_5_out);
  and and_3 (and_3_out, not_1_out, not_3_out, not_4_out, not_5_out);
  and and_4 (and_4_out, D4, D3, D2, D1);
  and and_5 (and_5_out, not_2_out, not_3_out, not_4_out, not_5_out);
  and and_6 (and_6_out, D5, not_2_out, D2, D1);
  and and_7 (and_7_out, D5, D3, D1);
  and and_8 (and_8_out, not_2_out, D3, not_6_out);
  and and_9 (and_9_out, D5, not_4_out, not_5_out, not_6_out);
  and and_10 (and_10_out, D5, D4, not_4_out, D0);
  and and_11 (and_11_out, not_1_out, D4, not_4_out, D1, not_6_out);
  and and_12 (and_12_out, D5, not_2_out, not_3_out, not_4_out, D1, not_6_out);
  and and_13 (and_13_out, not_1_out, not_3_out, D2, not_5_out, not_6_out);
  and and_14 (and_14_out, D5, D4, D2, D1);
  and and_15 (and_15_out, D4, not_3_out, D2, D1, D0);
  and and_16 (and_16_out, D4, D3, not_4_out, not_5_out);
  and and_17 (and_17_out, D5, not_2_out, not_3_out, not_4_out, D1, D0);
  and and_18 (and_18_out, not_1_out, not_2_out, not_3_out, D2, not_5_out, D0);
  and and_19 (and_19_out, D4, D3, D2, not_5_out, D0);
  and and_20 (and_20_out, D5, D4, not_4_out, D1, not_6_out);
  and and_21 (and_21_out, not_1_out, D4, not_3_out, not_4_out, D1, D0);
  and and_22 (and_22_out, D5, not_2_out, not_3_out, D2, not_5_out, not_6_out);
  and and_23 (and_23_out, D5, D4, D2, D0);
  and and_24 (and_24_out, not_1_out, not_3_out, D2, D1, not_6_out);
  and and_25 (and_25_out, D5, D3, not_5_out, D0);
  and and_26 (and_26_out, not_1_out, not_2_out, D3, D1, D0);
  and and_27 (and_27_out, D4, D3, D2, not_5_out, not_6_out);
  and and_28 (and_28_out, D5, not_2_out, not_3_out, D2, not_5_out, D0);
  and and_29 (and_29_out, not_1_out, not_2_out, not_3_out, D2, D1, D0);
  and and_30 (and_30_out, D4, D3, not_4_out, D1, D0);
  and and_31 (and_31_out, D5, D4, D2, not_5_out, not_6_out);
  and and_32 (and_32_out, not_1_out, D4, not_3_out, D2, not_5_out, D0);
  or or_1 (Db5, and_17_out, and_18_out, and_19_out);
  or or_2 (E5, and_28_out, and_29_out, and_30_out);
  or or_3 (G4, and_31_out, and_32_out);
  or or_4 (Fsharp5, and_1_out, and_2_out, and_3_out, and_4_out, and_5_out, and_6_out, and_7_out, and_8_out, and_9_out);
  or or_5 (B4, and_10_out, and_11_out, and_12_out, and_13_out, and_14_out, and_15_out, and_16_out);
  or or_6 (re5, and_20_out, and_21_out, and_22_out, and_23_out, and_24_out, and_25_out, and_26_out, and_27_out);
endmodule

module song2 (
  input  on_off,
  input  CLk,
  output pin2_buzzer,
  output Fsharp5,
  output B4,
  output Db5,
  output re5,
  output E5,
  output G4
);

  wire d_ff_1_q, d_ff_1_qn, d_ff_2_q, d_ff_2_qn, d_ff_3_q, d_ff_3_qn, d_ff_4_q, d_ff_4_qn, d_ff_5_q,
       d_ff_5_qn, d_ff_6_q, d_ff_6_qn, not_1_out, song2_64k_frequence_1_song2_note,
       song2_fsm_transition_logic_1_d0, song2_fsm_transition_logic_1_d1, song2_fsm_transition_logic_1_d2,
       song2_fsm_transition_logic_1_d3, song2_fsm_transition_logic_1_d4, song2_fsm_transition_logic_1_d5;

  not not_1 (not_1_out, on_off);
  song2_fsm_transition_logic song2_fsm_transition_logic_1 (
    .C5(d_ff_1_q), .C4(d_ff_2_q), .C3(d_ff_3_q), .C2(d_ff_4_q), .C1(d_ff_5_q), .C0(d_ff_6_q),
    .D5(song2_fsm_transition_logic_1_d5), .D4(song2_fsm_transition_logic_1_d4),
    .D3(song2_fsm_transition_logic_1_d3), .D2(song2_fsm_transition_logic_1_d2),
    .D1(song2_fsm_transition_logic_1_d1), .D0(song2_fsm_transition_logic_1_d0));
  D_Flip_Flop d_ff_1 (
    .D(song2_fsm_transition_logic_1_d5), .clk(CLk), .Q(d_ff_1_q), .Qn(d_ff_1_qn), .reset(not_1_out));  // open: preset
  D_Flip_Flop d_ff_2 (
    .D(song2_fsm_transition_logic_1_d4), .clk(CLk), .Q(d_ff_2_q), .Qn(d_ff_2_qn), .reset(not_1_out));  // open: preset
  D_Flip_Flop d_ff_3 (
    .D(song2_fsm_transition_logic_1_d3), .clk(CLk), .Q(d_ff_3_q), .Qn(d_ff_3_qn), .reset(not_1_out));  // open: preset
  D_Flip_Flop d_ff_4 (
    .D(song2_fsm_transition_logic_1_d2), .clk(CLk), .Q(d_ff_4_q), .Qn(d_ff_4_qn), .reset(not_1_out));  // open: preset
  D_Flip_Flop d_ff_5 (
    .D(song2_fsm_transition_logic_1_d1), .clk(CLk), .Q(d_ff_5_q), .Qn(d_ff_5_qn), .reset(not_1_out));  // open: preset
  D_Flip_Flop d_ff_6 (
    .D(song2_fsm_transition_logic_1_d0), .clk(CLk), .Q(d_ff_6_q), .Qn(d_ff_6_qn), .reset(not_1_out));  // open: preset
  // NoConnect on d_ff_1_qn
  // NoConnect on d_ff_2_qn
  // NoConnect on d_ff_3_qn
  // NoConnect on d_ff_4_qn
  // NoConnect on d_ff_5_qn
  // NoConnect on d_ff_6_qn
  song2_decoder song2_decoder_1 (
    .D5(d_ff_1_q), .D4(d_ff_2_q), .D3(d_ff_3_q), .D2(d_ff_4_q), .D1(d_ff_5_q), .D0(d_ff_6_q),
    .Fsharp5(Fsharp5), .B4(B4), .Db5(Db5), .re5(re5), .E5(E5), .G4(G4));
  song2_64k_frequence song2_64k_frequence_1 (
    .Fsharp5(Fsharp5), .B4(B4), .Db5(Db5), .re5(re5), .E5(E5), .G4(G4),
    .song2_note(song2_64k_frequence_1_song2_note));
  and and_1 (pin2_buzzer, song2_64k_frequence_1_song2_note, on_off);
endmodule

module song2_64k_frequence (
  input  Fsharp5,
  input  B4,
  input  Db5,
  input  re5,
  input  E5,
  input  G4,
  output song2_note
);

  wire and_1_out, and_2_out, and_3_out, and_4_out, and_5_out, and_6_out, B4_clock_out, Db5_clock_out,
       E5_clock_out, Fsharp5_clock_out, G4_clock_out, re5_clock_out;

  Clock #(.highDuration(43), .lowDuration(43)) Fsharp5_clock (.out(Fsharp5_clock_out));
  Clock #(.highDuration(65), .lowDuration(65)) B4_clock (.out(B4_clock_out));
  Clock #(.highDuration(58), .lowDuration(58)) Db5_clock (.out(Db5_clock_out));
  Clock #(.highDuration(54), .lowDuration(54)) re5_clock (.out(re5_clock_out));
  Clock #(.highDuration(49), .lowDuration(49)) E5_clock (.out(E5_clock_out));
  Clock #(.highDuration(82), .lowDuration(82)) G4_clock (.out(G4_clock_out));
  and and_1 (and_1_out, Fsharp5, Fsharp5_clock_out);
  and and_2 (and_2_out, B4, B4_clock_out);
  and and_3 (and_3_out, Db5, Db5_clock_out);
  and and_4 (and_4_out, re5, re5_clock_out);
  and and_5 (and_5_out, E5, E5_clock_out);
  and and_6 (and_6_out, G4, G4_clock_out);
  or or_1 (song2_note, and_1_out, and_2_out, and_3_out, and_4_out, and_5_out, and_6_out);
endmodule

module testig (
  input  CHA_PIN4,
  input  CHB_PIN5,
  input  Reset
);

  wire button_1_out, CCW, clock_1_out, clock_2_out, clock_3_out, clock_4_out, CW, d_ff_1_q, d_ff_2_q,
       d_ff_3_q;

  Clock clock_1 (.out(clock_1_out));
  Decoder_Rotation decoder_rotation_1 (
    .CHA(CHA_PIN4), .CHB(CHB_PIN5), .CLK(clock_1_out), .Reset(Reset), .CCW(CW), .CW(CCW));
  Button button_1 (.out(button_1_out));
  Clock clock_2 (.out(clock_2_out));
  D_Flip_Flop d_ff_1 (.D(button_1_out), .clk(clock_2_out), .Q(d_ff_1_q), .reset(Reset));  // open: Qn, preset
  D_Flip_Flop d_ff_2 (.D(d_ff_1_q), .clk(clock_3_out), .Q(d_ff_2_q), .reset(Reset));  // open: Qn, preset
  Clock #(.highDuration(2), .lowDuration(2)) clock_3 (.out(clock_3_out));
  D_Flip_Flop d_ff_3 (.D(d_ff_2_q), .clk(clock_4_out), .Q(d_ff_3_q));  // open: Qn, preset, reset
  Clock #(.highDuration(3), .lowDuration(3)) clock_4 (.out(clock_4_out));
  D_Flip_Flop d_ff_4 (.D(d_ff_3_q));  // open: clk, Q, Qn, preset, reset

  // Notes on the sheet:
  //   can use a counter...
  //   each D-ff delays the pulse by 1 tick but im gonna need 32000 of them... not viable 
endmodule

module glitch_free_clock_MUX (
  input  SELECTTT,
  input  CLK1,
  input  CLK2,
  input  reset,
  output CLK_OUT
);

  wire and_1_out, and_2_out, and_3_out, and_4_out, d_ff_1_q, d_ff_1_qn, d_ff_2_q, d_ff_2_qn, d_ff_3_q,
       d_ff_3_qn, d_ff_4_q, d_ff_4_qn;

  and and_1 (and_1_out, ~SELECTTT, ~d_ff_4_q);  // AND_Gate
  and and_2 (and_2_out, ~d_ff_3_q, SELECTTT);  // AND_Gate
  D_Flip_Flop d_ff_1 (.D(and_1_out), .clk(CLK1), .Q(d_ff_1_q), .Qn(d_ff_1_qn), .reset(reset));  // open: preset
  D_Flip_Flop d_ff_2 (.D(and_2_out), .clk(CLK2), .Q(d_ff_2_q), .Qn(d_ff_2_qn), .reset(reset));  // open: preset
  // NoConnect on d_ff_1_qn
  // NoConnect on d_ff_2_qn
  D_Flip_Flop d_ff_3 (.D(d_ff_1_q), .clk(CLK1), .Q(d_ff_3_q), .Qn(d_ff_3_qn), .reset(reset));  // open: preset
  D_Flip_Flop d_ff_4 (.D(d_ff_2_q), .clk(CLK2), .Q(d_ff_4_q), .Qn(d_ff_4_qn), .reset(reset));  // open: preset
  // NoConnect on d_ff_3_qn
  // NoConnect on d_ff_4_qn
  and and_3 (and_3_out, d_ff_3_q, CLK1);
  and and_4 (and_4_out, d_ff_4_q, CLK2);
  or or_1 (CLK_OUT, and_3_out, and_4_out);

  // Notes on the sheet:
  //   clock glitch free MUX 
endmodule

module glitch_free_mux_v2 (
  input  SELECTT,
  input  CLK1,
  input  CLK0,
  input  Reset,
  output CLK_OUT
);

  wire and_1_out, and_2_out, and_3_out, and_4_out, d_ff_1_q, d_ff_2_q, d_ff_2_qn, d_ff_3_q, d_ff_3_qn,
       d_ff_4_q, d_ff_4_qn, not_1_out, not_2_out, not_3_out;

  not not_1 (not_1_out, SELECTT);
  and and_1 (and_1_out, SELECTT, d_ff_4_qn);
  and and_2 (and_2_out, d_ff_3_qn, not_1_out);
  D_Flip_Flop d_ff_1 (.D(and_1_out), .clk(CLK1), .Q(d_ff_1_q), .reset(Reset));  // open: Qn, preset
  D_Flip_Flop d_ff_2 (.D(and_2_out), .clk(CLK0), .Q(d_ff_2_q), .Qn(d_ff_2_qn), .reset(Reset));  // open: preset
  // NoConnect on d_ff_2_qn
  D_Flip_Flop d_ff_3 (.D(d_ff_1_q), .clk(not_2_out), .Q(d_ff_3_q), .Qn(d_ff_3_qn), .reset(Reset));  // open: preset
  not not_2 (not_2_out, CLK1);
  not not_3 (not_3_out, CLK0);
  D_Flip_Flop d_ff_4 (.D(d_ff_2_q), .clk(not_3_out), .Q(d_ff_4_q), .Qn(d_ff_4_qn), .reset(Reset));  // open: preset
  and and_3 (and_3_out, d_ff_3_q, CLK1);
  and and_4 (and_4_out, d_ff_4_q, CLK0);
  or or_1 (CLK_OUT, and_3_out, and_4_out);
endmodule

module testing_press (
  input  Reset,
  input  CH_3_Pin6,
  output Vcc,
  output GND
);

  wire bouncing_filter_11_signal_out, CLK, clock_1_out, clock_3_out, not_1_out, toggle_button_3_outputtt;

  Clock clock_1 (.out(clock_1_out));
  Clock clock_2 (.out(CLK));
  not not_1 (not_1_out, CH_3_Pin6);
  LED debug1 (.in(bouncing_filter_11_signal_out));
  bouncing_filter bouncing_filter_11 (
    .INPUT_SIGNAL(not_1_out), .CLK(clock_1_out), .RESET(Reset), .SIGNAL_OUT(bouncing_filter_11_signal_out));
  Clock clock_3 (.out(clock_3_out));
  LED debugggggg (.in(toggle_button_3_outputtt));
  toggle_button toggle_button_3 (
    .Buttonn(bouncing_filter_11_signal_out), .CLK(clock_3_out), .Reset(Reset),
    .outputtt(toggle_button_3_outputtt));

  assign GND = 1'b0;
  assign Vcc = 1'b1;
endmodule
